// Logisim project cpu28_pred.circ as structural Verilog: 19 circuits, main circuit ◇动态分支预测
module \流水线MIPS  (
);

  wire and_1_out, and_2_out, and_3_out, and_4_out, and_5_out, and_6_out, and_7_out, and_9_out, Beq, Blez,
       Bne, Branch, BubbleClr, CLK, comparator_1_eq, Disp, EN, Equal, Ex_MemToReg, \ex_mem流水接口_1_halt_2 ,
       \ex_mem流水接口_1_jal_2 , \ex_mem流水接口_1_memwrite_2 , \ex_mem流水接口_1_regdst_2 , \ex_mem流水接口_1_sb_2 ,
       Ex_RegWrite, Go, Halt, HaltOrRST, ID_EX_Clr, ID_EX_EN, \id_ex流水接口_1_alusrcb_2 , \id_ex流水接口_1_halt_2 ,
       \id_ex流水接口_1_jal_2 , \id_ex流水接口_1_memwrite_2 , \id_ex流水接口_1_regdst_2 , \id_ex流水接口_1_sb_2 ,
       \id_ex流水接口_1_signedext_2 , IF_ID_EN, JMP, JR, Lez, LoadUse, Mem_MemToReg, Mem_RegWrite,
       \mem_wb流水接口_1_halt_2 , \mem_wb流水接口_1_jal_2 , \mem_wb流水接口_1_regdst_2 , MemWrite, not_1_out, not_2_out,
       not_3_out, not_5_out, not_6_out, not_7_out, R1_Used, R2_Used, RegWrite, RST, \硬布线控制器_1_alu_src ,
       \硬布线控制器_1_beq , \硬布线控制器_1_blez , \硬布线控制器_1_bne , \硬布线控制器_1_jal , \硬布线控制器_1_jmp , \硬布线控制器_1_jr ,
       \硬布线控制器_1_memtoreg , \硬布线控制器_1_regdst , \硬布线控制器_1_regwrite , \硬布线控制器_1_sb , \硬布线控制器_1_signedext ,
       \硬布线控制器_1_syscall ;
  wire [1:0] R1_Forward, R2_Forward, StoreForward;
  wire [3:0] decoder_1_out0, \id_ex流水接口_1_aluop_2 , multiplexer_19_out, \硬布线控制器_1_alu_op ;
  wire [4:0] Ex_WriteReg_num, Mem_WriteReg_num, multiplexer_6_out, multiplexer_7_out, multiplexer_10_out,
       multiplexer_16_out, R1_num, R2_num;
  wire [15:0] \LoadUse气泡数 , \总周期数 , \无条件分支数 , \条件分支成功数 ;
  wire [27:2] JmpAddr;
  wire [31:0] AluA, AluB, and_8_out, bit_extender_1_out, BranchAddr, CNT, Ex_Alu, \ex_mem流水接口_1_b_2 ,
       \ex_mem流水接口_1_ir_2 , EX_PC, \id_ex流水接口_1_b_2 , \id_ex流水接口_1_imm_2 , ID_PC, \if_id流水接口_1_ir , IF_PC,
       LedData, Mem_Alu, MEM_PC, Mem_ReadData, \mem_wb流水接口_1_ir_2 , mips_alu_1_result, mips_ram_1_p8,
       mips_regifile_1_r1, mips_regifile_1_r2, multiplexer_1_out, multiplexer_2_out, multiplexer_3_out,
       multiplexer_8_out, multiplexer_12_out, multiplexer_13_out, multiplexer_14_out, multiplexer_17_out,
       multiplexer_20_out, PC_q, R1, rom_1_data, shifter_1_out, WB_PC;
  wire [31:26] \id_ex流水接口_1_ir_2 ;

  Button \u_总复位  (.out(RST));
  Button u_Go (.out(Go));
  Clock clock_1 (.out(CLK));
  Multiplexer #(.width(32), .enable("false")) multiplexer_1 (
    .in0(multiplexer_2_out), .in1(multiplexer_3_out), .out(multiplexer_1_out), .sel(JMP));
  Multiplexer #(.width(32), .enable("false")) multiplexer_2 (
    .in0(IF_PC), .in1(BranchAddr), .out(multiplexer_2_out), .sel(Branch));
  Multiplexer #(.width(32), .enable("false")) multiplexer_3 (
    .in0({EX_PC[31:28], JmpAddr, 2'b00}), .in1(R1), .out(multiplexer_3_out), .sel(JR));
  not not_1 (not_1_out, Equal);
  Hex_Digit_Display hex_digit_display_1 (.value(LedData[27:24]));  // open: dp
  Hex_Digit_Display hex_digit_display_2 (.value(LedData[31:28]));  // open: dp
  Register #(.width(32)) PC (.D(multiplexer_1_out), .en(IF_ID_EN), .Q(PC_q), .clk(CLK), .clr(RST));
  and and_1 (and_1_out, Beq, Equal);
  and and_2 (and_2_out, Bne, not_1_out);
  and and_3 (and_3_out, Blez, Lez);
  Counter #(.width(16), .max('hffff)) counter_1 (.count(EN), .Q(\总周期数 ), .clk(CLK), .clr(RST));  // open: load, D, carry
  Hex_Digit_Display hex_digit_display_3 (.value(LedData[19:16]));  // open: dp
  Hex_Digit_Display hex_digit_display_4 (.value(LedData[23:20]));  // open: dp
  not not_2 (not_2_out, Halt);
  or or_1 (Branch, and_1_out, and_2_out, and_3_out);
  Hex_Digit_Display hex_digit_display_5 (.value(LedData[11:8]));  // open: dp
  Hex_Digit_Display hex_digit_display_6 (.value(LedData[15:12]));  // open: dp
  ROM #(.addrWidth(10), .dataWidth(32)) rom_1 (.addr(PC_q[11:2]), .data(rom_1_data));  // open: sel
  Adder #(.width(32)) adder_1 (.a(PC_q), .b(32'h4), .out(IF_PC));  // open: cin, cout
  \数据相关检测  \u_数据相关检测_1  (
    .R1_Used(R1_Used), .R1_num(R1_num), .R2_Used(R2_Used), .R2_num(R2_num),
    .Ex_WrtieReg_num(Ex_WriteReg_num), .Ex_RegWrite(Ex_RegWrite), .Ex_MemToReg(Ex_MemToReg),
    .Mem_WrtieReg_num(Mem_WriteReg_num), .Mem_RegWrite(Mem_RegWrite), .Mem_MemToReg(Mem_MemToReg),
    .MemWrite(MemWrite), .EN(not_2_out), .CLK(CLK), .RST(HaltOrRST), .LoadUse(LoadUse),
    .R1_Forward(R1_Forward), .R2_Forward(R2_Forward), .StoreForward(StoreForward));
  and and_4 (and_4_out, EN, ID_EX_EN, not_3_out);
  not not_3 (not_3_out, LoadUse);
  not not_4 (ID_EX_EN, Halt);
  and and_5 (and_5_out, Halt, Go);
  Counter #(.width(16), .max('hffff)) counter_2 (
    .count(and_6_out), .Q(\无条件分支数 ), .clk(CLK), .clr(RST));  // open: load, D, carry
  and and_6 (and_6_out, JMP, IF_ID_EN);
  Hex_Digit_Display hex_digit_display_7 (.value(LedData[7:4]));  // open: dp
  Hex_Digit_Display hex_digit_display_8 (.value(LedData[3:0]));  // open: dp
  or or_2 (BubbleClr, JMP, Branch);
  or or_3 (ID_EX_Clr, BubbleClr, LoadUse);
  or or_4 (IF_ID_EN, and_4_out, and_5_out);
  \IF_ID流水接口  \if_id流水接口_1  (
    .Inst(rom_1_data), .PC(IF_PC), .CLK(CLK), .IR(\if_id流水接口_1_ir ), .PC_2(ID_PC), .clr(BubbleClr),
    .EN(IF_ID_EN), .RST(RST));  // open: PC_, PC__2, Pred, Pred_2
  and and_7 (and_7_out, Branch, EN);
  // Probe on \总周期数 
  // Probe on \无条件分支数 
  // Probe on \条件分支成功数 
  \源寄存器控制器  \u_源寄存器控制器_1  (
    .OP(\if_id流水接口_1_ir [31:26]), .Func(\if_id流水接口_1_ir [5:0]), .R1_Used(R1_Used), .R2_Used(R2_Used));
  Multiplexer #(.width(5), .enable("false")) multiplexer_4 (
    .in0(\if_id流水接口_1_ir [25:21]), .in1(5'b00010), .out(R1_num), .sel(\硬布线控制器_1_syscall ));
  Multiplexer #(.width(5), .enable("false")) multiplexer_5 (
    .in0(\if_id流水接口_1_ir [20:16]), .in1(5'b00100), .out(R2_num), .sel(\硬布线控制器_1_syscall ));
  Multiplexer #(.width(5), .enable("false")) multiplexer_6 (
    .in0(\mem_wb流水接口_1_ir_2 [20:16]), .in1(\mem_wb流水接口_1_ir_2 [15:11]), .out(multiplexer_6_out),
    .sel(\mem_wb流水接口_1_regdst_2 ));
  Multiplexer #(.width(5), .enable("false")) multiplexer_7 (
    .in0(multiplexer_6_out), .in1({5{1'b1}}), .out(multiplexer_7_out), .sel(\mem_wb流水接口_1_jal_2 ));
  Counter #(.width(16), .max('hffff)) counter_3 (
    .count(and_7_out), .Q(\条件分支成功数 ), .clk(CLK), .clr(RST));  // open: load, D, carry
  \硬布线控制器  \u_硬布线控制器_1  (
    .Func(\if_id流水接口_1_ir [5:0]), .OP(\if_id流水接口_1_ir [31:26]), .ALU_OP(\硬布线控制器_1_alu_op ),
    .MemToReg(\硬布线控制器_1_memtoreg ), .MemWrite(MemWrite), .ALU_SRC(\硬布线控制器_1_alu_src ),
    .RegWrite(\硬布线控制器_1_regwrite ), .SysCALL(\硬布线控制器_1_syscall ), .SignedExt(\硬布线控制器_1_signedext ),
    .RegDst(\硬布线控制器_1_regdst ), .JR(\硬布线控制器_1_jr ), .JMP(\硬布线控制器_1_jmp ), .Beq(\硬布线控制器_1_beq ),
    .JAL(\硬布线控制器_1_jal ), .Bne(\硬布线控制器_1_bne ), .SB(\硬布线控制器_1_sb ), .BLEZ(\硬布线控制器_1_blez ));
  assign bit_extender_1_out = {{16{\if_id流水接口_1_ir [15]}}, \if_id流水接口_1_ir [15:0]};  // Bit_Extender bit_extender_1
  Multiplexer #(.width(32), .enable("false")) multiplexer_8 (
    .in0(Mem_ReadData), .in1(WB_PC), .out(multiplexer_8_out), .sel(\mem_wb流水接口_1_jal_2 ));
  // Probe on \LoadUse气泡数 
  MIPS_Regifile mips_regifile_1 (
    .Din(multiplexer_8_out), .Clk(CLK), .R1(mips_regifile_1_r1), .R2(mips_regifile_1_r2), .WE(RegWrite),
    .W_num(multiplexer_7_out), .R1_num(R1_num), .R2_num(R2_num));
  Register #(.width(32)) register_1 (.D(AluB), .en(Disp), .Q(LedData), .clk(CLK), .clr(RST));
  \ID_EX流水接口  \id_ex流水接口_1  (
    .RegWrite(\硬布线控制器_1_regwrite ), .RegDst(\硬布线控制器_1_regdst ), .JAL(\硬布线控制器_1_jal ), .SB(\硬布线控制器_1_sb ),
    .MemToReg(\硬布线控制器_1_memtoreg ), .MemWrite(MemWrite), .AluOp(\硬布线控制器_1_alu_op ),
    .AluSrcB(\硬布线控制器_1_alu_src ), .SignedExt(\硬布线控制器_1_signedext ), .Halt(\硬布线控制器_1_syscall ),
    .JMP(\硬布线控制器_1_jmp ), .JR(\硬布线控制器_1_jr ), .Beq(\硬布线控制器_1_beq ), .Bne(\硬布线控制器_1_bne ),
    .Blez(\硬布线控制器_1_blez ), .IR(\if_id流水接口_1_ir ), .PC(ID_PC), .A(mips_regifile_1_r1),
    .B(mips_regifile_1_r2), .Imm(bit_extender_1_out), .CLK(CLK), .RegWrite_2(Ex_RegWrite),
    .RegDst_2(\id_ex流水接口_1_regdst_2 ), .JAL_2(\id_ex流水接口_1_jal_2 ), .SB_2(\id_ex流水接口_1_sb_2 ),
    .MemToReg_2(Ex_MemToReg), .MemWrite_2(\id_ex流水接口_1_memwrite_2 ), .AluOp_2(\id_ex流水接口_1_aluop_2 ),
    .AluSrcB_2(\id_ex流水接口_1_alusrcb_2 ), .SignedExt_2(\id_ex流水接口_1_signedext_2 ),
    .Halt_2(\id_ex流水接口_1_halt_2 ), .JMP_2(JMP), .JR_2(JR), .Beq_2(Beq), .Bne_2(Bne), .Blez_2(Blez),
    .IR_2({\id_ex流水接口_1_ir_2 , JmpAddr}), .PC_2(EX_PC), .A_2(R1), .B_2(\id_ex流水接口_1_b_2 ),
    .Imm_2(\id_ex流水接口_1_imm_2 ), .clr(ID_EX_Clr), .EN(ID_EX_EN), .RST(HaltOrRST));  // open: PC_, PC__2, Pred, Pred_2
  assign and_8_out = \id_ex流水接口_1_imm_2  & 32'hffff;  // AND_Gate and_8, 32 bits wide
  Multiplexer #(.select(2), .width(32), .enable("false")) multiplexer_9 (
    .in0(R1), .in1(Mem_ReadData), .in2(Mem_Alu), .in3(Ex_Alu), .out(AluA), .sel(R1_Forward));
  Counter #(.width(16), .max('hffff)) counter_4 (
    .count(and_9_out), .Q(\LoadUse气泡数 ), .clk(CLK), .clr(RST));  // open: load, D, carry
  and and_9 (and_9_out, LoadUse, EN);
  Multiplexer #(.width(5), .enable("false")) multiplexer_10 (
    .in0(JmpAddr[22:18]), .in1(JmpAddr[17:13]), .out(multiplexer_10_out), .sel(\id_ex流水接口_1_regdst_2 ));
  Multiplexer #(.width(5), .enable("false")) multiplexer_11 (
    .in0(multiplexer_10_out), .in1({5{1'b1}}), .out(Ex_WriteReg_num), .sel(\id_ex流水接口_1_jal_2 ));
  Multiplexer #(.width(32), .enable("false")) multiplexer_12 (
    .in0(\id_ex流水接口_1_b_2 ), .in1(multiplexer_13_out), .out(multiplexer_12_out), .sel(\id_ex流水接口_1_alusrcb_2 ));
  Multiplexer #(.width(32), .enable("false")) multiplexer_13 (
    .in0(and_8_out), .in1(\id_ex流水接口_1_imm_2 ), .out(multiplexer_13_out), .sel(\id_ex流水接口_1_signedext_2 ));
  // Mips_Probe mips_probe_1: pin names not known; wires that end beside it: {\id_ex流水接口_1_ir_2 , JmpAddr}
  Shifter #(.width(32)) shifter_1 (.in(\id_ex流水接口_1_imm_2 ), .\dist (5'b00010), .out(shifter_1_out));
  Multiplexer #(.select(2), .width(32), .enable("false")) multiplexer_14 (
    .in0(\id_ex流水接口_1_b_2 ), .in1(Mem_ReadData), .in2(Mem_Alu), .in3(Ex_Alu), .out(multiplexer_14_out),
    .sel(StoreForward));
  Multiplexer #(.select(2), .width(32), .enable("false")) multiplexer_15 (
    .in0(multiplexer_12_out), .in1(Mem_ReadData), .in2(Mem_Alu), .in3(Ex_Alu), .out(AluB), .sel(R2_Forward));
  Adder #(.width(32)) adder_2 (.a(EX_PC), .b(shifter_1_out), .out(BranchAddr));  // open: cin, cout
  MIPS_ALU mips_alu_1 (
    .X(AluA), .Y(AluB), .AluOP(\id_ex流水接口_1_aluop_2 ), .Equal(Equal), .Result(mips_alu_1_result),
    .shamt(JmpAddr[12:8]), .LEZ(Lez));  // open: Result_2
  Counter #(.width(32), .max('hffffffff)) counter_5 (
    .count(EN), .Q(CNT), .clk(CLK), .clr(RST));  // open: load, D, carry
  // Probe on CNT
  Comparator #(.width(32)) comparator_1 (.a(AluA), .b(32'h22), .eq(comparator_1_eq));  // open: gt, lt
  \EX_MEM流水接口  \ex_mem流水接口_1  (
    .RegWrite(Ex_RegWrite), .RegDst(\id_ex流水接口_1_regdst_2 ), .JAL(\id_ex流水接口_1_jal_2 ),
    .SB(\id_ex流水接口_1_sb_2 ), .MemToReg(Ex_MemToReg), .MemWrite(\id_ex流水接口_1_memwrite_2 ),
    .IR({\id_ex流水接口_1_ir_2 , JmpAddr}), .PC(EX_PC), .ALU(mips_alu_1_result), .B(multiplexer_14_out),
    .CLK(CLK), .RegWrite_2(Mem_RegWrite), .RegDst_2(\ex_mem流水接口_1_regdst_2 ), .JAL_2(\ex_mem流水接口_1_jal_2 ),
    .SB_2(\ex_mem流水接口_1_sb_2 ), .MemToReg_2(Mem_MemToReg), .MemWrite_2(\ex_mem流水接口_1_memwrite_2 ),
    .IR_2(\ex_mem流水接口_1_ir_2 ), .PC_2(MEM_PC), .ALU_2(Ex_Alu), .B_2(\ex_mem流水接口_1_b_2 ), .clr(1'b0), .EN(EN),
    .Halt(Halt), .Halt_2(\ex_mem流水接口_1_halt_2 ), .RST(HaltOrRST));
  Decoder #(.select(2), .enable("false")) decoder_1 (
    .out0(decoder_1_out0[0]), .out1(decoder_1_out0[1]), .out2(decoder_1_out0[2]), .out3(decoder_1_out0[3]),
    .sel(Ex_Alu[1:0]));
  and and_10 (Disp, comparator_1_eq, \id_ex流水接口_1_halt_2 );
  not not_5 (not_5_out, comparator_1_eq);
  Multiplexer #(.width(5), .enable("false")) multiplexer_16 (
    .in0(\ex_mem流水接口_1_ir_2 [20:16]), .in1(\ex_mem流水接口_1_ir_2 [15:11]), .out(multiplexer_16_out),
    .sel(\ex_mem流水接口_1_regdst_2 ));
  Multiplexer #(.width(32), .enable("false")) multiplexer_17 (
    .in0(\ex_mem流水接口_1_b_2 ),
    .in1({\ex_mem流水接口_1_b_2 [7:0], \ex_mem流水接口_1_b_2 [7:0], \ex_mem流水接口_1_b_2 [7:0], \ex_mem流水接口_1_b_2 [7:0]}),
    .out(multiplexer_17_out), .sel(\ex_mem流水接口_1_sb_2 ));
  and and_11 (Halt, not_5_out, \id_ex流水接口_1_halt_2 );
  Multiplexer #(.width(5), .enable("false")) multiplexer_18 (
    .in0(multiplexer_16_out), .in1({5{1'b1}}), .out(Mem_WriteReg_num), .sel(\ex_mem流水接口_1_jal_2 ));
  Multiplexer #(.width(4), .enable("false")) multiplexer_19 (
    .in0(4'b1111), .in1(decoder_1_out0), .out(multiplexer_19_out), .sel(\ex_mem流水接口_1_sb_2 ));
  // Probe on IF_PC[11:0]
  // Probe on ID_PC[11:0]
  // Probe on EX_PC[11:0]
  // Probe on MEM_PC[11:0]
  // Probe on WB_PC[11:0]
  // MIPS_RAM mips_ram_1: pin names not known; wires that end beside it: Ex_Alu[11:2], multiplexer_17_out, \ex_mem流水接口_1_memwrite_2 , multiplexer_19_out, CLK, 1'b1, RST, mips_ram_1_p8
  Multiplexer #(.width(32), .enable("false")) multiplexer_20 (
    .in0(Ex_Alu), .in1(mips_ram_1_p8), .out(multiplexer_20_out), .sel(Mem_MemToReg));
  \MEM_WB流水接口  \mem_wb流水接口_1  (
    .RegWrite(Mem_RegWrite), .RegDst(\ex_mem流水接口_1_regdst_2 ), .JAL(\ex_mem流水接口_1_jal_2 ),
    .IR(\ex_mem流水接口_1_ir_2 ), .PC(MEM_PC), .ALU(Ex_Alu), .MD(multiplexer_20_out), .CLK(CLK),
    .RegWrite_2(RegWrite), .RegDst_2(\mem_wb流水接口_1_regdst_2 ), .JAL_2(\mem_wb流水接口_1_jal_2 ),
    .IR_2(\mem_wb流水接口_1_ir_2 ), .PC_2(WB_PC), .ALU_2(Mem_Alu), .MD_2(Mem_ReadData), .clr(1'b0), .EN(EN),
    .Halt(\ex_mem流水接口_1_halt_2 ), .Halt_2(\mem_wb流水接口_1_halt_2 ), .RST(RST));
  not not_6 (not_6_out, Go);
  not not_7 (not_7_out, EN);
  nand nand_1 (EN, \mem_wb流水接口_1_halt_2 , not_6_out);
  or or_5 (HaltOrRST, not_7_out, RST);

  // Other names for the same wires on the sheet: JmpAddr[31:28] = EX_PC[31:28]; IF_ID_Clr = BubbleClr;
  //   PC_EN = IF_ID_EN

  // Notes on the sheet:
  //   数码管输出应该用寄存器锁存，否则显示数据只能一闪而过
  //   可以通过项目增加Logisim库的方式将前几次实验完成的电路作为子电路引入到本电路中使用
  //   指令存储器
  //   contents of rom_1 (hex, n*v repeats v):
  //   20110001 8000c05 20110001 20120002 20130003 8000c09 20110001 20120002 20130003 8000c0d 20110001
  //   20120002 20130003 8000c11 20110001 20120002 20130003 c000cf5 20100001 20110001 118fc0 112020
  //   20020022 c 118882 12200001 8000c15 112020 20020022 c 20110001 118880 112020 20020022 c 12200001
  //   8000c1f 20110001 118fc0 112020 20020022 c 1188c3 112020 20020022 c 118903 112020 20020022 c 118903
  //   112020 20020022 c 118903 112020 20020022 c 118903 112020 20020022 c 118903 112020 20020022 c 118903
  //   112020 20020022 c 118903 112020 20020022 c 20100001 109fc0 139fc3 8021 2012000c 24160003 26100001
  //   3210000f 20080008 20090001 139900 2709825 132020 20020022 c 1094022 1500fff9 22100001 2018000f
  //   2188024 108700 20080008 20090001 139902 2709825 132021 20020022 c 1094022 1500fff9 108702 2c9b022
  //   12c00001 8000c50 4020 1084027 84400 3508ffff 82021 20020022 c 2010ffff 20110000 ae300000 22100001
  //   22310004 ae300000 22100001 22310004 ae300000 22100001 22310004 ae300000 22100001 22310004 ae300000
  //   22100001 22310004 ae300000 22100001 22310004 ae300000 22100001 22310004 ae300000 22100001 22310004
  //   ae300000 22100001 22310004 ae300000 22100001 22310004 ae300000 22100001 22310004 ae300000 22100001
  //   22310004 ae300000 22100001 22310004 ae300000 22100001 22310004 ae300000 22100001 22310004 ae300000
  //   22100001 22310004 22100001 8020 2011003c 8e130000 8e340000 274402a 11000002 ae330000 ae140000
  //   2231fffc 1611fff8 102020 20020022 c 22100004 2011003c 1611fff2 20020032 c 2008ffff 20117777 112020
  //   20020022 c 200b0010 2288826 112020 20020022 c 216bffff 1560fffa 2002000a c 2008ffff 20117777 112020
  //   20020022 c 200b0010 3a31ffff 112020 20020022 c 216bffff 1560fffa 2002000a c 20090000 200b0020
  //   20110000 20120001 a1310000 112020 20020022 c 2328820 21290001 216bffff 1560fff8 200b0008 20090000
  //   8d310000 112020 20020022 c 21290004 216bffff 1560fff9 2002000a c 2011fff1 112020 20020022 c 22310001
  //   1a20fffb 2002000a c 2002000a c 20100000 22100001 102020 20020022 c 22100002 102020 20020022 c
  //   22100003 102020 20020022 c 22100004 102020 20020022 c 22100005 102020 20020022 c 22100006 102020
  //   20020022 c 22100007 102020 20020022 c 22100008 102020 20020022 20020022 c 3e00008
  //   数码管输出
  //   指令字
  //   总复位信号应将除ROM以外所有存储组件全部清零
endmodule

module \单周期MIPS  (
);

  wire AluSrcB, and_2_out, and_5_out, and_6_out, and_7_out, and_8_out, BELZ, Beq, Bne, Branch, CLK,
       comparator_1_eq, Disp, EN, Equal, Go, JAL, JMP, JR, LEZ, MemToReg, MemWrite, not_1_out, not_2_out,
       not_4_out, RegDst, RegWrite, RST, SB, SignedExt, Syscall;
  wire [1:0] MemBias;
  wire [3:0] AluOP;
  wire [4:0] multiplexer_4_out, multiplexer_5_out, multiplexer_6_out, multiplexer_7_out;
  wire [5:0] Func, OP;
  wire [15:0] \总周期数 , \无条件分支数 , \条件分支成功数 ;
  wire [15:6] Imm;
  wire [27:0] adder_1_out;
  wire [31:0] adder_2_out, and_3_out, and_4_out, LedData, MemIn, MemOut, multiplexer_1_out,
       multiplexer_2_out, multiplexer_3_out, multiplexer_9_out, multiplexer_10_out, multiplexer_11_out,
       multiplexer_12_out, not_3_out, or_1_out, PC_q, R1, R2, shifter_1_out, shifter_2_out, shifter_3_out,
       Signed;
  wire [31:2] mips_alu_1_result;
  wire [31:18] adder_1_out_2;

  Button \u_总复位  (.out(RST));
  Button u_Go (.out(Go));
  Clock clock_1 (.out(CLK));
  Multiplexer #(.width(32), .enable("false")) multiplexer_1 (
    .in0({adder_1_out_2[31:28], adder_1_out}), .in1(adder_2_out), .out(multiplexer_1_out), .sel(Branch));
  Multiplexer #(.width(32), .enable("false")) multiplexer_2 (
    .in0(multiplexer_1_out), .in1(multiplexer_3_out), .out(multiplexer_2_out), .sel(JMP));
  Counter #(.width(16), .max('hffff)) counter_1 (.count(EN), .Q(\总周期数 ), .clk(CLK), .clr(RST));  // open: load, D, carry
  Hex_Digit_Display hex_digit_display_1 (.value(LedData[31:28]));  // open: dp
  Hex_Digit_Display hex_digit_display_2 (.value(LedData[27:24]));  // open: dp
  not not_1 (not_1_out, Go);
  Comparator #(.width(32)) comparator_1 (.a(R1), .b(32'h22), .eq(comparator_1_eq));  // open: gt, lt
  Register #(.width(32)) PC (.D(multiplexer_2_out), .en(EN), .Q(PC_q), .clk(CLK), .clr(RST));
  Multiplexer #(.width(32), .enable("false")) multiplexer_3 (
    .in0({adder_1_out_2, Imm, Func, 2'b00}), .in1(R1), .out(multiplexer_3_out), .sel(JR));
  Hex_Digit_Display hex_digit_display_3 (.value(LedData[19:16]));  // open: dp
  Hex_Digit_Display hex_digit_display_4 (.value(LedData[23:20]));  // open: dp
  not not_2 (not_2_out, comparator_1_eq);
  and and_1 (Disp, Syscall, comparator_1_eq);
  Adder #(.width(32)) adder_1 (.a(PC_q), .b(32'h4), .out({adder_1_out_2[31:28], adder_1_out}));  // open: cin, cout
  and and_2 (and_2_out, JMP, EN);
  assign and_3_out = 32'hff & R2;  // AND_Gate and_3, 32 bits wide
  Hex_Digit_Display hex_digit_display_5 (.value(LedData[15:12]));  // open: dp
  Hex_Digit_Display hex_digit_display_6 (.value(LedData[11:8]));  // open: dp
  nand nand_1 (EN, not_1_out, not_2_out, Syscall);
  ROM #(.addrWidth(10), .dataWidth(32)) rom_1 (
    .addr(PC_q[11:2]), .data({OP, adder_1_out_2[27:18], Imm, Func}));  // open: sel
  Counter #(.width(16), .max('hffff)) counter_2 (
    .count(and_2_out), .Q(\无条件分支数 ), .clk(CLK), .clr(RST));  // open: load, D, carry
  Shifter #(.width(32)) shifter_1 (.in(and_3_out), .\dist ({MemBias, 3'b000}), .out(shifter_1_out));
  Shifter #(.width(32)) shifter_2 (.in(32'hff), .\dist ({MemBias, 3'b000}), .out(shifter_2_out));
  Hex_Digit_Display hex_digit_display_7 (.value(LedData[3:0]));  // open: dp
  Hex_Digit_Display hex_digit_display_8 (.value(LedData[7:4]));  // open: dp
  // Mips_Probe mips_probe_1: pin names not known; wires that end beside it: {OP, adder_1_out_2[27:18], Imm, Func}
  assign and_4_out = MemOut & not_3_out;  // AND_Gate and_4, 32 bits wide
  assign not_3_out = ~shifter_2_out;  // NOT_Gate not_3, 32 bits wide
  Multiplexer #(.width(5), .enable("false")) multiplexer_4 (
    .in0(adder_1_out_2[27:23]), .in1(5'b00010), .out(multiplexer_4_out), .sel(Syscall));
  Multiplexer #(.width(5), .enable("false")) multiplexer_5 (
    .in0(adder_1_out_2[22:18]), .in1(Imm[15:11]), .out(multiplexer_5_out), .sel(RegDst));
  assign or_1_out = shifter_1_out | and_4_out;  // OR_Gate or_1, 32 bits wide
  Multiplexer #(.width(5), .enable("false")) multiplexer_6 (
    .in0(adder_1_out_2[22:18]), .in1(5'b00100), .out(multiplexer_6_out), .sel(Disp));
  Multiplexer #(.width(5), .enable("false")) multiplexer_7 (
    .in0(multiplexer_5_out), .in1({5{1'b1}}), .out(multiplexer_7_out), .sel(JAL));
  Counter #(.width(16), .max('hffff)) counter_3 (
    .count(and_5_out), .Q(\条件分支成功数 ), .clk(CLK), .clr(RST));  // open: load, D, carry
  and and_5 (and_5_out, Branch, EN);
  Multiplexer #(.width(32), .enable("false")) multiplexer_8 (.in0(R2), .in1(or_1_out), .out(MemIn), .sel(SB));
  // Probe on \总周期数 
  // Probe on \无条件分支数 
  // Probe on \条件分支成功数 
  MIPS_Regifile mips_regifile_1 (
    .Din(multiplexer_9_out), .Clk(CLK), .R1(R1), .R2(R2), .WE(RegWrite), .W_num(multiplexer_7_out),
    .R1_num(multiplexer_4_out), .R2_num(multiplexer_6_out));
  Multiplexer #(.width(32), .enable("false")) multiplexer_9 (
    .in0(multiplexer_12_out), .in1({adder_1_out_2[31:28], adder_1_out}), .out(multiplexer_9_out), .sel(JAL));
  Multiplexer #(.width(32), .enable("false")) multiplexer_10 (
    .in0(R2), .in1(multiplexer_11_out), .out(multiplexer_10_out), .sel(AluSrcB));
  Multiplexer #(.width(32), .enable("false")) multiplexer_11 (
    .in0({{16{1'b0}}, Imm, Func}), .in1(Signed), .out(multiplexer_11_out), .sel(SignedExt));
  MIPS_ALU mips_alu_1 (
    .X(R1), .Y(multiplexer_10_out), .AluOP(AluOP), .Equal(Equal), .Result({mips_alu_1_result, MemBias}),
    .shamt(Imm[10:6]), .LEZ(LEZ));  // open: Result_2
  Shifter #(.width(32)) shifter_3 (.in(Signed), .\dist (5'b00010), .out(shifter_3_out));
  Register #(.width(32)) register_1 (.D(R2), .en(Disp), .Q(LedData), .clk(CLK), .clr(RST));
  \硬布线控制器  \u_硬布线控制器_1  (
    .Func(Func), .OP(OP), .ALU_OP(AluOP), .MemToReg(MemToReg), .MemWrite(MemWrite), .ALU_SRC(AluSrcB),
    .RegWrite(RegWrite), .SysCALL(Syscall), .SignedExt(SignedExt), .RegDst(RegDst), .JR(JR), .JMP(JMP),
    .Beq(Beq), .JAL(JAL), .Bne(Bne), .SB(SB), .BLEZ(BELZ));
  Adder #(.width(32)) adder_2 (
    .a(shifter_3_out), .b({adder_1_out_2[31:28], adder_1_out}), .out(adder_2_out));  // open: cin, cout
  and and_6 (and_6_out, Beq, Equal);
  and and_7 (and_7_out, Bne, not_4_out);
  not not_4 (not_4_out, Equal);
  and and_8 (and_8_out, BELZ, LEZ);
  RAM #(.addrWidth(10), .dataWidth(32), .bus("separate")) ram_1 (
    .addr(mips_alu_1_result[11:2]), .din(MemIn), .data(MemOut), .str(MemWrite), .clk(CLK), .ld(1'b1),
    .clr(RST));  // open: sel
  assign Signed = {{16{Imm[15]}}, {Imm, Func}};  // Bit_Extender bit_extender_1
  or or_2 (Branch, and_6_out, and_7_out, and_8_out);
  Multiplexer #(.width(32), .enable("false")) multiplexer_12 (
    .in0({mips_alu_1_result, MemBias}), .in1(MemOut), .out(multiplexer_12_out), .sel(MemToReg));

  // Other names for the same wires on the sheet: Imm[5:0] = Func; ZeroExt[15:0] = {Imm, Func}; Shamt[4:0] = Imm[10:6]

  // Notes on the sheet:
  //   数码管输出应该用寄存器锁存，否则显示数据只能一闪而过
  //   可以通过项目增加Logisim库的方式将前几次实验完成的电路作为子电路引入到本电路中使用
  //   指令存储器
  //   contents of rom_1 (hex, n*v repeats v):
  //   20110001 8000c05 20110001 20120002 20130003 8000c09 20110001 20120002 20130003 8000c0d 20110001
  //   20120002 20130003 8000c11 20110001 20120002 20130003 c000cf5 20100001 20110001 118fc0 112020
  //   20020022 c 118882 12200001 8000c15 112020 20020022 c 20110001 118880 112020 20020022 c 12200001
  //   8000c1f 20110001 118fc0 112020 20020022 c 1188c3 112020 20020022 c 118903 112020 20020022 c 118903
  //   112020 20020022 c 118903 112020 20020022 c 118903 112020 20020022 c 118903 112020 20020022 c 118903
  //   112020 20020022 c 118903 112020 20020022 c 20100001 109fc0 139fc3 8021 2012000c 24160003 26100001
  //   3210000f 20080008 20090001 139900 2709825 132020 20020022 c 1094022 1500fff9 22100001 2018000f
  //   2188024 108700 20080008 20090001 139902 2709825 132021 20020022 c 1094022 1500fff9 108702 2c9b022
  //   12c00001 8000c50 4020 1084027 84400 3508ffff 82021 20020022 c 2010ffff 20110000 ae300000 22100001
  //   22310004 ae300000 22100001 22310004 ae300000 22100001 22310004 ae300000 22100001 22310004 ae300000
  //   22100001 22310004 ae300000 22100001 22310004 ae300000 22100001 22310004 ae300000 22100001 22310004
  //   ae300000 22100001 22310004 ae300000 22100001 22310004 ae300000 22100001 22310004 ae300000 22100001
  //   22310004 ae300000 22100001 22310004 ae300000 22100001 22310004 ae300000 22100001 22310004 ae300000
  //   22100001 22310004 22100001 8020 2011003c 8e130000 8e340000 274402a 11000002 ae330000 ae140000
  //   2231fffc 1611fff8 102020 20020022 c 22100004 2011003c 1611fff2 20020032 c 2008ffff 20117777 112020
  //   20020022 c 200b0010 2288826 112020 20020022 c 216bffff 1560fffa 2002000a c 2008ffff 20117777 112020
  //   20020022 c 200b0010 3a31ffff 112020 20020022 c 216bffff 1560fffa 2002000a c 20090000 200b0020
  //   20110000 20120001 a1310000 112020 20020022 c 2328820 21290001 216bffff 1560fff8 200b0008 20090000
  //   8d310000 112020 20020022 c 21290004 216bffff 1560fff9 2002000a c 2011fff1 112020 20020022 c 22310001
  //   1a20fffb 2002000a c 2002000a c 20100000 22100001 102020 20020022 c 22100002 102020 20020022 c
  //   22100003 102020 20020022 c 22100004 102020 20020022 c 22100005 102020 20020022 c 22100006 102020
  //   20020022 c 22100007 102020 20020022 c 22100008 102020 20020022 20020022 c 3e00008
  //   数码管输出
  //   OP
  //   Func
  //   rs
  //   指令字
  //   rt
  //   rd
  //   总复位信号应将除ROM以外所有存储组件全部清零
  //   JMP
  //   JR
  //   OP
  //   Func
  //   Beq
  //   Bne
  //   MemToReg
  //   MemWrite
  //   AluOP
  //   AluSrcB
  //   RegWrite
  //   JAL
  //   RegDst
  //   Syscall
endmodule

// 单周期硬布线控制器
module \硬布线控制器  (
  input  [5:0] OP,
  input  [5:0] Func,
  output [3:0] ALU_OP,
  output MemToReg,
  output MemWrite,
  output ALU_SRC,
  output RegWrite,
  output SysCALL,
  output SignedExt,
  output RegDst,
  output Beq,
  output Bne,
  output JR,
  output JMP,
  output JAL,
  output SB,
  output BLEZ
);

  \运算控制器  \u_运算控制器_1  (
    .OP0(OP[0]), .OP1(OP[1]), .OP2(OP[2]), .OP3(OP[3]), .OP4(OP[4]), .OP5(OP[5]), .F0(Func[0]), .F1(Func[1]),
    .F2(Func[2]), .F3(Func[3]), .F4(Func[4]), .F5(Func[5]), .S0(ALU_OP[0]), .S1(ALU_OP[1]), .S2(ALU_OP[2]),
    .S3(ALU_OP[3]));
  \控制信号生成  \u_控制信号生成_1  (
    .OP0(OP[0]), .OP1(OP[1]), .OP2(OP[2]), .OP3(OP[3]), .OP4(OP[4]), .OP5(OP[5]), .F0(Func[0]), .F1(Func[1]),
    .F2(Func[2]), .F3(Func[3]), .F4(Func[4]), .F5(Func[5]), .MemToReg(MemToReg), .MemWrite(MemWrite),
    .ALU_SRC(ALU_SRC), .RegWrite(RegWrite), .SysCALL(SysCALL), .SignedExt(SignedExt), .RegDst(RegDst),
    .BEQ(Beq), .BNE(Bne), .JR(JR), .JMP(JMP), .JAL(JAL));
  \附加控制信号  \u_附加控制信号_1  (
    .OP0(OP[0]), .OP1(OP[1]), .OP2(OP[2]), .OP3(OP[3]), .OP4(OP[4]), .OP5(OP[5]), .SB(SB), .BLEZ(BLEZ));

  // Other names for the same wires on the sheet: OP_CODE[5:0] = OP

  // Notes on the sheet:
  //   运算器控制器，根据指令生成运算器功能选择信号
  //   控制信号生成，产生数据通路需要的其他控制信号
endmodule

// 运算器控制器
module \运算控制器  (
  input  OP0,
  input  OP1,
  input  OP2,
  input  OP3,
  input  OP4,
  input  OP5,
  input  F0,
  input  F1,
  input  F2,
  input  F3,
  input  F4,
  input  F5,
  output S0,
  output S1,
  output S2,
  output S3
);

  wire and_1_out, and_2_out, and_3_out, and_4_out, and_5_out, and_6_out, and_7_out, and_8_out, and_9_out,
       and_10_out, and_11_out, and_12_out, and_13_out, and_14_out, and_15_out, and_16_out, and_17_out,
       and_18_out, and_19_out, and_20_out, and_21_out, and_22_out, and_23_out, and_24_out, and_25_out,
       and_26_out, and_27_out, and_28_out, and_29_out, and_30_out, and_31_out, and_32_out, and_33_out,
       and_34_out, and_35_out, and_36_out, and_37_out, and_38_out, and_39_out, and_40_out, not_1_out,
       not_2_out, not_3_out, not_4_out, not_5_out, not_6_out, not_7_out, not_8_out, not_9_out, not_10_out,
       not_11_out, not_12_out, not_13_out, not_14_out, not_15_out, not_16_out, not_17_out, not_18_out,
       not_19_out, not_20_out, not_21_out, not_22_out, not_23_out, not_24_out, not_25_out, not_26_out,
       not_27_out, not_28_out, not_29_out, not_30_out, not_31_out, not_32_out, not_33_out, not_34_out,
       not_35_out, not_36_out, not_37_out, not_38_out, not_39_out, not_40_out, not_41_out, not_42_out,
       not_43_out, not_44_out, not_45_out, not_46_out, not_47_out, not_48_out, not_49_out, not_50_out,
       not_51_out, not_52_out, not_53_out, not_54_out, not_55_out, not_56_out, not_57_out, not_58_out,
       not_59_out, not_60_out, not_61_out, not_62_out, not_63_out, not_64_out, not_65_out, not_66_out,
       not_67_out, not_68_out, not_69_out, not_70_out, not_71_out, not_72_out, not_73_out, not_74_out,
       not_75_out, not_76_out, not_77_out, not_78_out, not_79_out, not_80_out, not_81_out, not_82_out,
       not_83_out, not_84_out, not_85_out, not_86_out, not_87_out, not_88_out, not_89_out, not_90_out,
       not_91_out, not_92_out, not_93_out, not_94_out, not_95_out, not_96_out, not_97_out, not_98_out,
       not_99_out, not_100_out, not_101_out, not_102_out, not_103_out, not_104_out, not_105_out, not_106_out,
       not_107_out, not_108_out, not_109_out, not_110_out, not_111_out, not_112_out, not_113_out,
       not_114_out, not_115_out, not_116_out, not_117_out, not_118_out, not_119_out, not_120_out,
       not_121_out, not_122_out, not_123_out, not_124_out, not_125_out, not_126_out, not_127_out,
       not_128_out, not_129_out, not_130_out, not_131_out, not_132_out, not_133_out, not_134_out,
       not_135_out, not_136_out, not_137_out, not_138_out, not_139_out, not_140_out, not_141_out,
       not_142_out, not_143_out, not_144_out, not_145_out, not_146_out, not_147_out, not_148_out,
       not_149_out, not_150_out, not_151_out, not_152_out, not_153_out, not_154_out, not_155_out,
       not_156_out, not_157_out, not_158_out, not_159_out, not_160_out, not_161_out, not_162_out,
       not_163_out, not_164_out, not_165_out, not_166_out, not_167_out, not_168_out, not_169_out,
       not_170_out, not_171_out, not_172_out, not_173_out, not_174_out, not_175_out, not_176_out,
       not_177_out, not_178_out, not_179_out, not_180_out, not_181_out, not_182_out, not_183_out,
       not_184_out, not_185_out, not_186_out, not_187_out, not_188_out, not_189_out, not_190_out,
       not_191_out, not_192_out, not_193_out, not_194_out, not_195_out, not_196_out, not_197_out,
       not_198_out, not_199_out, not_200_out, not_201_out, not_202_out, not_203_out, not_204_out,
       not_205_out, not_206_out, not_207_out, not_208_out, not_209_out, not_210_out, not_211_out,
       not_212_out, not_213_out, not_214_out, not_215_out, not_216_out, not_217_out, not_218_out,
       not_219_out, not_220_out, not_221_out, not_222_out, not_223_out, not_224_out, not_225_out,
       not_226_out, not_227_out, not_228_out, not_229_out, not_230_out, not_231_out, not_232_out,
       not_233_out, not_234_out, not_235_out, not_236_out, not_237_out, not_238_out, not_239_out,
       not_240_out, not_241_out, not_242_out, not_243_out, not_244_out, not_245_out, not_246_out,
       not_247_out, not_248_out, not_249_out, not_250_out, not_251_out, not_252_out, not_253_out,
       not_254_out, not_255_out, not_256_out, not_257_out, not_258_out, not_259_out, not_260_out,
       not_261_out, not_262_out, not_263_out, not_264_out, not_265_out, not_266_out, not_267_out, not_268_out;

  not not_1 (not_1_out, OP5);
  not not_2 (not_2_out, OP4);
  not not_3 (not_3_out, OP3);
  not not_4 (not_4_out, OP2);
  not not_5 (not_5_out, OP1);
  not not_6 (not_6_out, OP0);
  not not_7 (not_7_out, F5);
  not not_8 (not_8_out, F4);
  not not_9 (not_9_out, F3);
  not not_10 (not_10_out, F2);
  not not_11 (not_11_out, OP5);
  not not_12 (not_12_out, OP4);
  not not_13 (not_13_out, OP3);
  not not_14 (not_14_out, OP2);
  not not_15 (not_15_out, OP1);
  not not_16 (not_16_out, OP0);
  not not_17 (not_17_out, F4);
  not not_18 (not_18_out, F3);
  not not_19 (not_19_out, F2);
  not not_20 (not_20_out, F1);
  not not_21 (not_21_out, F0);
  not not_22 (not_22_out, OP5);
  not not_23 (not_23_out, OP4);
  not not_24 (not_24_out, OP3);
  not not_25 (not_25_out, OP2);
  not not_26 (not_26_out, OP1);
  not not_27 (not_27_out, OP0);
  not not_28 (not_28_out, F4);
  not not_29 (not_29_out, F3);
  not not_30 (not_30_out, F2);
  not not_31 (not_31_out, F1);
  not not_32 (not_32_out, OP5);
  not not_33 (not_33_out, OP4);
  not not_34 (not_34_out, OP3);
  not not_35 (not_35_out, OP2);
  not not_36 (not_36_out, OP1);
  not not_37 (not_37_out, OP0);
  not not_38 (not_38_out, F4);
  not not_39 (not_39_out, F3);
  not not_40 (not_40_out, F1);
  not not_41 (not_41_out, F0);
  not not_42 (not_42_out, OP5);
  not not_43 (not_43_out, OP4);
  not not_44 (not_44_out, OP3);
  not not_45 (not_45_out, OP2);
  not not_46 (not_46_out, OP1);
  not not_47 (not_47_out, OP0);
  not not_48 (not_48_out, F4);
  not not_49 (not_49_out, F2);
  not not_50 (not_50_out, F0);
  not not_51 (not_51_out, OP5);
  not not_52 (not_52_out, OP4);
  not not_53 (not_53_out, OP2);
  not not_54 (not_54_out, OP1);
  not not_55 (not_55_out, OP0);
  not not_56 (not_56_out, OP5);
  not not_57 (not_57_out, OP4);
  not not_58 (not_58_out, OP1);
  not not_59 (not_59_out, OP0);
  not not_60 (not_60_out, OP5);
  not not_61 (not_61_out, OP4);
  not not_62 (not_62_out, OP2);
  not not_63 (not_63_out, OP1);
  not not_64 (not_64_out, OP5);
  not not_65 (not_65_out, OP4);
  not not_66 (not_66_out, OP2);
  not not_67 (not_67_out, OP0);
  not not_68 (not_68_out, OP4);
  not not_69 (not_69_out, OP3);
  not not_70 (not_70_out, OP2);
  not not_71 (not_71_out, OP4);
  not not_72 (not_72_out, OP2);
  not not_73 (not_73_out, OP5);
  not not_74 (not_74_out, OP4);
  not not_75 (not_75_out, OP3);
  not not_76 (not_76_out, OP2);
  not not_77 (not_77_out, OP1);
  not not_78 (not_78_out, OP0);
  not not_79 (not_79_out, F4);
  not not_80 (not_80_out, F3);
  not not_81 (not_81_out, F0);
  not not_82 (not_82_out, OP5);
  not not_83 (not_83_out, OP4);
  not not_84 (not_84_out, OP0);
  not not_85 (not_85_out, OP4);
  not not_86 (not_86_out, OP2);
  not not_87 (not_87_out, OP1);
  not not_88 (not_88_out, OP0);
  not not_89 (not_89_out, OP5);
  not not_90 (not_90_out, OP4);
  not not_91 (not_91_out, OP3);
  not not_92 (not_92_out, OP2);
  not not_93 (not_93_out, OP1);
  not not_94 (not_94_out, OP0);
  not not_95 (not_95_out, F5);
  not not_96 (not_96_out, F4);
  not not_97 (not_97_out, F3);
  not not_98 (not_98_out, F2);
  not not_99 (not_99_out, F0);
  not not_100 (not_100_out, OP5);
  not not_101 (not_101_out, OP4);
  not not_102 (not_102_out, OP3);
  not not_103 (not_103_out, OP2);
  not not_104 (not_104_out, OP1);
  not not_105 (not_105_out, OP0);
  not not_106 (not_106_out, F4);
  not not_107 (not_107_out, F3);
  not not_108 (not_108_out, F2);
  not not_109 (not_109_out, F0);
  not not_110 (not_110_out, OP5);
  not not_111 (not_111_out, OP4);
  not not_112 (not_112_out, OP3);
  not not_113 (not_113_out, OP2);
  not not_114 (not_114_out, OP1);
  not not_115 (not_115_out, OP0);
  not not_116 (not_116_out, F4);
  not not_117 (not_117_out, F3);
  not not_118 (not_118_out, F1);
  not not_119 (not_119_out, F0);
  not not_120 (not_120_out, OP5);
  not not_121 (not_121_out, OP4);
  not not_122 (not_122_out, OP3);
  not not_123 (not_123_out, OP2);
  not not_124 (not_124_out, OP1);
  not not_125 (not_125_out, OP0);
  not not_126 (not_126_out, F4);
  not not_127 (not_127_out, F3);
  not not_128 (not_128_out, OP5);
  not not_129 (not_129_out, OP4);
  not not_130 (not_130_out, OP3);
  not not_131 (not_131_out, OP2);
  not not_132 (not_132_out, OP1);
  not not_133 (not_133_out, OP0);
  not not_134 (not_134_out, F4);
  not not_135 (not_135_out, F2);
  not not_136 (not_136_out, F0);
  not not_137 (not_137_out, OP5);
  not not_138 (not_138_out, OP4);
  not not_139 (not_139_out, OP1);
  not not_140 (not_140_out, OP0);
  not not_141 (not_141_out, OP5);
  not not_142 (not_142_out, OP4);
  not not_143 (not_143_out, OP2);
  not not_144 (not_144_out, OP0);
  not not_145 (not_145_out, OP5);
  not not_146 (not_146_out, OP4);
  not not_147 (not_147_out, OP3);
  not not_148 (not_148_out, OP2);
  not not_149 (not_149_out, OP1);
  not not_150 (not_150_out, OP0);
  not not_151 (not_151_out, F4);
  not not_152 (not_152_out, F3);
  not not_153 (not_153_out, F2);
  not not_154 (not_154_out, F1);
  not not_155 (not_155_out, F0);
  not not_156 (not_156_out, OP5);
  not not_157 (not_157_out, OP4);
  not not_158 (not_158_out, OP3);
  not not_159 (not_159_out, OP2);
  not not_160 (not_160_out, OP1);
  not not_161 (not_161_out, OP0);
  not not_162 (not_162_out, F4);
  not not_163 (not_163_out, F3);
  not not_164 (not_164_out, F2);
  not not_165 (not_165_out, F1);
  not not_166 (not_166_out, OP5);
  not not_167 (not_167_out, OP4);
  not not_168 (not_168_out, OP3);
  not not_169 (not_169_out, OP2);
  not not_170 (not_170_out, OP1);
  not not_171 (not_171_out, OP0);
  not not_172 (not_172_out, F4);
  not not_173 (not_173_out, F3);
  not not_174 (not_174_out, F2);
  not not_175 (not_175_out, F0);
  not not_176 (not_176_out, OP5);
  not not_177 (not_177_out, OP4);
  not not_178 (not_178_out, OP3);
  not not_179 (not_179_out, OP2);
  not not_180 (not_180_out, OP1);
  not not_181 (not_181_out, OP0);
  not not_182 (not_182_out, F4);
  not not_183 (not_183_out, F3);
  not not_184 (not_184_out, F1);
  not not_185 (not_185_out, F0);
  not not_186 (not_186_out, OP5);
  not not_187 (not_187_out, OP4);
  not not_188 (not_188_out, OP3);
  not not_189 (not_189_out, OP2);
  not not_190 (not_190_out, OP1);
  not not_191 (not_191_out, OP0);
  not not_192 (not_192_out, F4);
  not not_193 (not_193_out, F2);
  not not_194 (not_194_out, OP5);
  not not_195 (not_195_out, OP4);
  not not_196 (not_196_out, OP2);
  not not_197 (not_197_out, OP1);
  not not_198 (not_198_out, OP0);
  not not_199 (not_199_out, OP5);
  not not_200 (not_200_out, OP4);
  not not_201 (not_201_out, OP1);
  not not_202 (not_202_out, OP0);
  not not_203 (not_203_out, OP5);
  not not_204 (not_204_out, OP4);
  not not_205 (not_205_out, OP2);
  not not_206 (not_206_out, OP1);
  not not_207 (not_207_out, OP4);
  not not_208 (not_208_out, OP3);
  not not_209 (not_209_out, OP2);
  not not_210 (not_210_out, OP4);
  not not_211 (not_211_out, OP2);
  not not_212 (not_212_out, OP4);
  not not_213 (not_213_out, OP2);
  not not_214 (not_214_out, OP1);
  not not_215 (not_215_out, OP0);
  not not_216 (not_216_out, OP5);
  not not_217 (not_217_out, OP4);
  not not_218 (not_218_out, OP3);
  not not_219 (not_219_out, OP2);
  not not_220 (not_220_out, OP1);
  not not_221 (not_221_out, OP0);
  not not_222 (not_222_out, F4);
  not not_223 (not_223_out, F3);
  not not_224 (not_224_out, F1);
  not not_225 (not_225_out, OP5);
  not not_226 (not_226_out, OP4);
  not not_227 (not_227_out, OP3);
  not not_228 (not_228_out, OP2);
  not not_229 (not_229_out, OP1);
  not not_230 (not_230_out, OP0);
  not not_231 (not_231_out, F4);
  not not_232 (not_232_out, F3);
  not not_233 (not_233_out, OP5);
  not not_234 (not_234_out, OP4);
  not not_235 (not_235_out, OP3);
  not not_236 (not_236_out, OP2);
  not not_237 (not_237_out, OP1);
  not not_238 (not_238_out, OP0);
  not not_239 (not_239_out, F4);
  not not_240 (not_240_out, F2);
  not not_241 (not_241_out, F0);
  not not_242 (not_242_out, OP5);
  not not_243 (not_243_out, OP4);
  not not_244 (not_244_out, OP3);
  not not_245 (not_245_out, OP2);
  not not_246 (not_246_out, OP1);
  not not_247 (not_247_out, OP0);
  not not_248 (not_248_out, F4);
  not not_249 (not_249_out, F2);
  not not_250 (not_250_out, OP5);
  not not_251 (not_251_out, OP4);
  not not_252 (not_252_out, OP2);
  not not_253 (not_253_out, OP0);
  not not_254 (not_254_out, OP5);
  not not_255 (not_255_out, OP4);
  not not_256 (not_256_out, OP1);
  not not_257 (not_257_out, OP5);
  not not_258 (not_258_out, OP4);
  not not_259 (not_259_out, OP3);
  not not_260 (not_260_out, OP2);
  not not_261 (not_261_out, OP1);
  not not_262 (not_262_out, OP0);
  not not_263 (not_263_out, F4);
  not not_264 (not_264_out, F3);
  not not_265 (not_265_out, F0);
  not not_266 (not_266_out, OP5);
  not not_267 (not_267_out, OP4);
  not not_268 (not_268_out, OP0);
  and and_1 (and_1_out, not_1_out, not_2_out, not_3_out, not_4_out, not_5_out, not_6_out, not_7_out, not_8_out, not_9_out, not_10_out, F1, F0);
  and and_2 (and_2_out, not_11_out, not_12_out, not_13_out, not_14_out, not_15_out, not_16_out, F5, not_17_out, not_18_out, not_19_out, not_20_out, not_21_out);
  and and_3 (and_3_out, not_22_out, not_23_out, not_24_out, not_25_out, not_26_out, not_27_out, F5, not_28_out, not_29_out, not_30_out, not_31_out, F0);
  and and_4 (and_4_out, not_32_out, not_33_out, not_34_out, not_35_out, not_36_out, not_37_out, F5, not_38_out, not_39_out, F2, not_40_out, not_41_out);
  and and_5 (and_5_out, not_42_out, not_43_out, not_44_out, not_45_out, not_46_out, not_47_out, F5, not_48_out, F3, not_49_out, F1, not_50_out);
  and and_6 (and_6_out, not_51_out, not_52_out, OP3, not_53_out, not_54_out, not_55_out);
  and and_7 (and_7_out, not_56_out, not_57_out, OP3, OP2, not_58_out, not_59_out);
  and and_8 (and_8_out, not_60_out, not_61_out, OP3, not_62_out, not_63_out, OP0);
  and and_9 (and_9_out, not_64_out, not_65_out, OP3, not_66_out, OP1, not_67_out);
  and and_10 (and_10_out, OP5, not_68_out, not_69_out, not_70_out, OP1, OP0);
  and and_11 (and_11_out, OP5, not_71_out, OP3, not_72_out, OP1, OP0);
  and and_12 (and_12_out, not_73_out, not_74_out, not_75_out, not_76_out, not_77_out, not_78_out, F5, not_79_out, not_80_out, F2, F1, not_81_out);
  and and_13 (and_13_out, not_82_out, not_83_out, OP3, OP2, OP1, not_84_out);
  and and_14 (and_14_out, OP5, not_85_out, OP3, not_86_out, not_87_out, not_88_out);
  and and_15 (and_15_out, not_89_out, not_90_out, not_91_out, not_92_out, not_93_out, not_94_out, not_95_out, not_96_out, not_97_out, not_98_out, F1, not_99_out);
  and and_16 (and_16_out, not_100_out, not_101_out, not_102_out, not_103_out, not_104_out, not_105_out, F5, not_106_out, not_107_out, not_108_out, F1, not_109_out);
  and and_17 (and_17_out, not_110_out, not_111_out, not_112_out, not_113_out, not_114_out, not_115_out, F5, not_116_out, not_117_out, F2, not_118_out, not_119_out);
  and and_18 (and_18_out, not_120_out, not_121_out, not_122_out, not_123_out, not_124_out, not_125_out, F5, not_126_out, not_127_out, F2, F1, F0);
  and and_19 (and_19_out, not_128_out, not_129_out, not_130_out, not_131_out, not_132_out, not_133_out, F5, not_134_out, F3, not_135_out, F1, not_136_out);
  and and_20 (and_20_out, not_137_out, not_138_out, OP3, OP2, not_139_out, not_140_out);
  and and_21 (and_21_out, not_141_out, not_142_out, OP3, not_143_out, OP1, not_144_out);
  and and_22 (and_22_out, not_145_out, not_146_out, not_147_out, not_148_out, not_149_out, not_150_out, F5, not_151_out, not_152_out, not_153_out, not_154_out, not_155_out);
  and and_23 (and_23_out, not_156_out, not_157_out, not_158_out, not_159_out, not_160_out, not_161_out, F5, not_162_out, not_163_out, not_164_out, not_165_out, F0);
  and and_24 (and_24_out, not_166_out, not_167_out, not_168_out, not_169_out, not_170_out, not_171_out, F5, not_172_out, not_173_out, not_174_out, F1, not_175_out);
  and and_25 (and_25_out, not_176_out, not_177_out, not_178_out, not_179_out, not_180_out, not_181_out, F5, not_182_out, not_183_out, F2, not_184_out, not_185_out);
  and and_26 (and_26_out, not_186_out, not_187_out, not_188_out, not_189_out, not_190_out, not_191_out, F5, not_192_out, F3, not_193_out, F1, F0);
  and and_27 (and_27_out, not_194_out, not_195_out, OP3, not_196_out, not_197_out, not_198_out);
  and and_28 (and_28_out, not_199_out, not_200_out, OP3, OP2, not_201_out, not_202_out);
  and and_29 (and_29_out, not_203_out, not_204_out, OP3, not_205_out, not_206_out, OP0);
  and and_30 (and_30_out, OP5, not_207_out, not_208_out, not_209_out, OP1, OP0);
  and and_31 (and_31_out, OP5, not_210_out, OP3, not_211_out, OP1, OP0);
  and and_32 (and_32_out, OP5, not_212_out, OP3, not_213_out, not_214_out, not_215_out);
  and and_33 (and_33_out, not_216_out, not_217_out, not_218_out, not_219_out, not_220_out, not_221_out, F5, not_222_out, not_223_out, F2, not_224_out, F0);
  and and_34 (and_34_out, not_225_out, not_226_out, not_227_out, not_228_out, not_229_out, not_230_out, F5, not_231_out, not_232_out, F2, F1, F0);
  and and_35 (and_35_out, not_233_out, not_234_out, not_235_out, not_236_out, not_237_out, not_238_out, F5, not_239_out, F3, not_240_out, F1, not_241_out);
  and and_36 (and_36_out, not_242_out, not_243_out, not_244_out, not_245_out, not_246_out, not_247_out, F5, not_248_out, F3, not_249_out, F1, F0);
  and and_37 (and_37_out, not_250_out, not_251_out, OP3, not_252_out, OP1, not_253_out);
  and and_38 (and_38_out, not_254_out, not_255_out, OP3, OP2, not_256_out, OP0);
  and and_39 (and_39_out, not_257_out, not_258_out, not_259_out, not_260_out, not_261_out, not_262_out, F5, not_263_out, not_264_out, F2, F1, not_265_out);
  and and_40 (and_40_out, not_266_out, not_267_out, OP3, OP2, OP1, not_268_out);
  or or_1 (S1, and_15_out, and_16_out, and_17_out, and_18_out, and_19_out, and_20_out, and_21_out);
  or or_2 (S2, and_22_out, and_23_out, and_24_out, and_25_out, and_26_out, and_27_out, and_28_out, and_29_out, and_30_out, and_31_out, and_32_out);
  or or_3 (S3, and_33_out, and_34_out, and_35_out, and_36_out, and_37_out, and_38_out, and_39_out, and_40_out);
  or or_4 (S0, and_1_out, and_2_out, and_3_out, and_4_out, and_5_out, and_6_out, and_7_out, and_8_out, and_9_out, and_10_out, and_11_out, and_12_out, and_13_out, and_14_out);
endmodule

// 控制信号生成
module \控制信号生成  (
  input  OP0,
  input  OP1,
  input  OP2,
  input  OP3,
  input  OP4,
  input  OP5,
  input  F0,
  input  F1,
  input  F2,
  input  F3,
  input  F4,
  input  F5,
  output MemToReg,
  output MemWrite,
  output ALU_SRC,
  output RegWrite,
  output SysCALL,
  output SignedExt,
  output RegDst,
  output BEQ,
  output BNE,
  output JR,
  output JMP,
  output JAL
);

  wire and_2_out, and_3_out, and_4_out, and_5_out, and_6_out, and_7_out, and_8_out, and_9_out, and_10_out,
       and_11_out, and_12_out, and_13_out, and_14_out, and_15_out, and_16_out, and_17_out, and_18_out,
       and_19_out, and_20_out, and_21_out, and_22_out, and_23_out, and_24_out, and_25_out, and_26_out,
       and_27_out, and_28_out, and_29_out, and_30_out, and_31_out, and_32_out, and_34_out, and_35_out,
       and_36_out, and_37_out, and_38_out, and_39_out, and_40_out, and_41_out, and_42_out, and_43_out,
       and_44_out, and_45_out, and_46_out, and_47_out, and_48_out, and_49_out, and_50_out, and_51_out,
       and_55_out, and_56_out, and_57_out, not_1_out, not_2_out, not_3_out, not_4_out, not_5_out, not_6_out,
       not_7_out, not_8_out, not_9_out, not_10_out, not_11_out, not_12_out, not_13_out, not_14_out,
       not_15_out, not_16_out, not_17_out, not_18_out, not_19_out, not_20_out, not_21_out, not_22_out,
       not_23_out, not_24_out, not_25_out, not_26_out, not_27_out, not_28_out, not_29_out, not_30_out,
       not_31_out, not_32_out, not_33_out, not_34_out, not_35_out, not_36_out, not_37_out, not_38_out,
       not_39_out, not_40_out, not_41_out, not_42_out, not_43_out, not_44_out, not_45_out, not_46_out,
       not_47_out, not_48_out, not_49_out, not_50_out, not_51_out, not_52_out, not_53_out, not_54_out,
       not_55_out, not_56_out, not_57_out, not_58_out, not_59_out, not_60_out, not_61_out, not_62_out,
       not_63_out, not_64_out, not_65_out, not_66_out, not_67_out, not_68_out, not_69_out, not_70_out,
       not_71_out, not_72_out, not_73_out, not_74_out, not_75_out, not_76_out, not_77_out, not_78_out,
       not_79_out, not_80_out, not_81_out, not_82_out, not_83_out, not_84_out, not_85_out, not_86_out,
       not_87_out, not_88_out, not_89_out, not_90_out, not_91_out, not_92_out, not_93_out, not_94_out,
       not_95_out, not_96_out, not_97_out, not_98_out, not_99_out, not_100_out, not_101_out, not_102_out,
       not_103_out, not_104_out, not_105_out, not_106_out, not_107_out, not_108_out, not_109_out,
       not_110_out, not_111_out, not_112_out, not_113_out, not_114_out, not_115_out, not_116_out,
       not_117_out, not_118_out, not_119_out, not_120_out, not_121_out, not_122_out, not_123_out,
       not_124_out, not_125_out, not_126_out, not_127_out, not_128_out, not_129_out, not_130_out,
       not_131_out, not_132_out, not_133_out, not_134_out, not_135_out, not_136_out, not_137_out,
       not_138_out, not_139_out, not_140_out, not_141_out, not_142_out, not_143_out, not_144_out,
       not_145_out, not_146_out, not_147_out, not_148_out, not_149_out, not_150_out, not_151_out,
       not_152_out, not_153_out, not_154_out, not_155_out, not_156_out, not_157_out, not_158_out,
       not_159_out, not_160_out, not_161_out, not_162_out, not_163_out, not_164_out, not_165_out,
       not_166_out, not_167_out, not_168_out, not_169_out, not_170_out, not_171_out, not_172_out,
       not_173_out, not_174_out, not_175_out, not_176_out, not_177_out, not_178_out, not_179_out,
       not_180_out, not_181_out, not_182_out, not_183_out, not_184_out, not_185_out, not_186_out,
       not_187_out, not_188_out, not_189_out, not_190_out, not_191_out, not_192_out, not_193_out,
       not_194_out, not_195_out, not_196_out, not_197_out, not_198_out, not_199_out, not_200_out,
       not_201_out, not_202_out, not_203_out, not_204_out, not_205_out, not_206_out, not_207_out,
       not_208_out, not_209_out, not_210_out, not_211_out, not_212_out, not_213_out, not_214_out,
       not_215_out, not_216_out, not_217_out, not_218_out, not_219_out, not_220_out, not_221_out,
       not_222_out, not_223_out, not_224_out, not_225_out, not_226_out, not_227_out, not_228_out,
       not_229_out, not_230_out, not_231_out, not_232_out, not_233_out, not_234_out, not_235_out,
       not_236_out, not_237_out, not_238_out, not_239_out, not_240_out, not_241_out, not_242_out,
       not_243_out, not_244_out, not_245_out, not_246_out, not_247_out, not_248_out, not_249_out,
       not_250_out, not_251_out, not_252_out, not_253_out, not_254_out, not_255_out, not_256_out,
       not_257_out, not_258_out, not_259_out, not_260_out, not_261_out, not_262_out, not_263_out,
       not_264_out, not_265_out, not_266_out, not_267_out, not_268_out, not_269_out, not_270_out,
       not_271_out, not_272_out, not_273_out, not_274_out, not_275_out, not_276_out, not_277_out,
       not_278_out, not_279_out, not_280_out, not_281_out, not_282_out, not_283_out, not_284_out,
       not_285_out, not_286_out, not_287_out, not_288_out, not_289_out, not_290_out, not_291_out,
       not_292_out, not_293_out, not_294_out, not_295_out, not_296_out, not_297_out, not_298_out,
       not_299_out, not_300_out, not_301_out, not_302_out, not_303_out, not_304_out, not_305_out,
       not_306_out, not_307_out, not_308_out, not_309_out, not_310_out, not_311_out, not_312_out,
       not_313_out, not_314_out, not_315_out, not_316_out, not_317_out, not_318_out, not_319_out,
       not_320_out, not_321_out, not_322_out, not_323_out, not_324_out, not_325_out, not_326_out,
       not_327_out, not_328_out, not_329_out, not_330_out, not_331_out, not_332_out, not_333_out,
       not_334_out, not_335_out, not_336_out, not_337_out, not_338_out, not_339_out, not_340_out,
       not_341_out, not_342_out, not_343_out, not_344_out, not_345_out, not_346_out, not_347_out,
       not_348_out, not_349_out, not_350_out, not_351_out, not_352_out, not_353_out, not_354_out,
       not_355_out, not_356_out, not_357_out, not_358_out, not_359_out, not_360_out, not_361_out,
       not_362_out, not_363_out, not_364_out, not_365_out, not_366_out, not_367_out, not_368_out,
       not_369_out, not_370_out, not_371_out, not_372_out, not_373_out, not_374_out, not_375_out,
       not_376_out, not_377_out, not_378_out, not_379_out, not_380_out, not_381_out;

  not not_1 (not_1_out, OP4);
  not not_2 (not_2_out, OP3);
  not not_3 (not_3_out, OP2);
  not not_4 (not_4_out, OP4);
  not not_5 (not_5_out, OP2);
  not not_6 (not_6_out, OP4);
  not not_7 (not_7_out, OP2);
  not not_8 (not_8_out, OP1);
  not not_9 (not_9_out, OP0);
  not not_10 (not_10_out, OP5);
  not not_11 (not_11_out, OP4);
  not not_12 (not_12_out, OP2);
  not not_13 (not_13_out, OP1);
  not not_14 (not_14_out, OP0);
  not not_15 (not_15_out, OP5);
  not not_16 (not_16_out, OP4);
  not not_17 (not_17_out, OP1);
  not not_18 (not_18_out, OP0);
  not not_19 (not_19_out, OP5);
  not not_20 (not_20_out, OP4);
  not not_21 (not_21_out, OP2);
  not not_22 (not_22_out, OP1);
  not not_23 (not_23_out, OP5);
  not not_24 (not_24_out, OP4);
  not not_25 (not_25_out, OP2);
  not not_26 (not_26_out, OP0);
  not not_27 (not_27_out, OP5);
  not not_28 (not_28_out, OP4);
  not not_29 (not_29_out, OP1);
  not not_30 (not_30_out, OP4);
  not not_31 (not_31_out, OP3);
  not not_32 (not_32_out, OP2);
  not not_33 (not_33_out, OP4);
  not not_34 (not_34_out, OP2);
  not not_35 (not_35_out, OP5);
  not not_36 (not_36_out, OP4);
  not not_37 (not_37_out, OP0);
  not not_38 (not_38_out, OP4);
  not not_39 (not_39_out, OP2);
  not not_40 (not_40_out, OP1);
  not not_41 (not_41_out, OP0);
  not not_42 (not_42_out, OP5);
  not not_43 (not_43_out, OP4);
  not not_44 (not_44_out, OP3);
  not not_45 (not_45_out, OP2);
  not not_46 (not_46_out, OP1);
  not not_47 (not_47_out, OP0);
  not not_48 (not_48_out, F5);
  not not_49 (not_49_out, F4);
  not not_50 (not_50_out, F3);
  not not_51 (not_51_out, F2);
  not not_52 (not_52_out, F1);
  not not_53 (not_53_out, F0);
  not not_54 (not_54_out, OP5);
  not not_55 (not_55_out, OP4);
  not not_56 (not_56_out, OP3);
  not not_57 (not_57_out, OP2);
  not not_58 (not_58_out, OP1);
  not not_59 (not_59_out, OP0);
  not not_60 (not_60_out, F5);
  not not_61 (not_61_out, F4);
  not not_62 (not_62_out, F3);
  not not_63 (not_63_out, F2);
  not not_64 (not_64_out, OP5);
  not not_65 (not_65_out, OP4);
  not not_66 (not_66_out, OP3);
  not not_67 (not_67_out, OP2);
  not not_68 (not_68_out, OP1);
  not not_69 (not_69_out, OP0);
  not not_70 (not_70_out, F5);
  not not_71 (not_71_out, F4);
  not not_72 (not_72_out, F3);
  not not_73 (not_73_out, F2);
  not not_74 (not_74_out, F0);
  not not_75 (not_75_out, OP5);
  not not_76 (not_76_out, OP4);
  not not_77 (not_77_out, OP3);
  not not_78 (not_78_out, OP2);
  not not_79 (not_79_out, OP1);
  not not_80 (not_80_out, OP0);
  not not_81 (not_81_out, F4);
  not not_82 (not_82_out, F3);
  not not_83 (not_83_out, F2);
  not not_84 (not_84_out, F1);
  not not_85 (not_85_out, F0);
  not not_86 (not_86_out, OP5);
  not not_87 (not_87_out, OP4);
  not not_88 (not_88_out, OP3);
  not not_89 (not_89_out, OP2);
  not not_90 (not_90_out, OP1);
  not not_91 (not_91_out, OP0);
  not not_92 (not_92_out, F4);
  not not_93 (not_93_out, F3);
  not not_94 (not_94_out, F2);
  not not_95 (not_95_out, F1);
  not not_96 (not_96_out, OP5);
  not not_97 (not_97_out, OP4);
  not not_98 (not_98_out, OP3);
  not not_99 (not_99_out, OP2);
  not not_100 (not_100_out, OP1);
  not not_101 (not_101_out, OP0);
  not not_102 (not_102_out, F4);
  not not_103 (not_103_out, F3);
  not not_104 (not_104_out, F2);
  not not_105 (not_105_out, F0);
  not not_106 (not_106_out, OP5);
  not not_107 (not_107_out, OP4);
  not not_108 (not_108_out, OP3);
  not not_109 (not_109_out, OP2);
  not not_110 (not_110_out, OP1);
  not not_111 (not_111_out, OP0);
  not not_112 (not_112_out, F4);
  not not_113 (not_113_out, F3);
  not not_114 (not_114_out, F1);
  not not_115 (not_115_out, F0);
  not not_116 (not_116_out, OP5);
  not not_117 (not_117_out, OP4);
  not not_118 (not_118_out, OP3);
  not not_119 (not_119_out, OP2);
  not not_120 (not_120_out, OP1);
  not not_121 (not_121_out, OP0);
  not not_122 (not_122_out, F4);
  not not_123 (not_123_out, F3);
  not not_124 (not_124_out, F1);
  not not_125 (not_125_out, OP5);
  not not_126 (not_126_out, OP4);
  not not_127 (not_127_out, OP3);
  not not_128 (not_128_out, OP2);
  not not_129 (not_129_out, OP1);
  not not_130 (not_130_out, OP0);
  not not_131 (not_131_out, F4);
  not not_132 (not_132_out, F3);
  not not_133 (not_133_out, OP5);
  not not_134 (not_134_out, OP4);
  not not_135 (not_135_out, OP3);
  not not_136 (not_136_out, OP2);
  not not_137 (not_137_out, OP1);
  not not_138 (not_138_out, OP0);
  not not_139 (not_139_out, F4);
  not not_140 (not_140_out, F2);
  not not_141 (not_141_out, F0);
  not not_142 (not_142_out, OP5);
  not not_143 (not_143_out, OP4);
  not not_144 (not_144_out, OP3);
  not not_145 (not_145_out, OP2);
  not not_146 (not_146_out, OP1);
  not not_147 (not_147_out, OP0);
  not not_148 (not_148_out, F4);
  not not_149 (not_149_out, F2);
  not not_150 (not_150_out, OP5);
  not not_151 (not_151_out, OP4);
  not not_152 (not_152_out, OP3);
  not not_153 (not_153_out, OP2);
  not not_154 (not_154_out, OP5);
  not not_155 (not_155_out, OP4);
  not not_156 (not_156_out, OP2);
  not not_157 (not_157_out, OP1);
  not not_158 (not_158_out, OP0);
  not not_159 (not_159_out, OP5);
  not not_160 (not_160_out, OP4);
  not not_161 (not_161_out, OP1);
  not not_162 (not_162_out, OP0);
  not not_163 (not_163_out, OP5);
  not not_164 (not_164_out, OP4);
  not not_165 (not_165_out, OP2);
  not not_166 (not_166_out, OP1);
  not not_167 (not_167_out, OP5);
  not not_168 (not_168_out, OP4);
  not not_169 (not_169_out, OP2);
  not not_170 (not_170_out, OP0);
  not not_171 (not_171_out, OP5);
  not not_172 (not_172_out, OP4);
  not not_173 (not_173_out, OP1);
  not not_174 (not_174_out, OP4);
  not not_175 (not_175_out, OP3);
  not not_176 (not_176_out, OP2);
  not not_177 (not_177_out, OP5);
  not not_178 (not_178_out, OP4);
  not not_179 (not_179_out, OP3);
  not not_180 (not_180_out, OP2);
  not not_181 (not_181_out, OP1);
  not not_182 (not_182_out, OP0);
  not not_183 (not_183_out, F4);
  not not_184 (not_184_out, F3);
  not not_185 (not_185_out, F0);
  not not_186 (not_186_out, OP5);
  not not_187 (not_187_out, OP4);
  not not_188 (not_188_out, OP0);
  not not_189 (not_189_out, OP5);
  not not_190 (not_190_out, OP4);
  not not_191 (not_191_out, OP3);
  not not_192 (not_192_out, OP2);
  not not_193 (not_193_out, OP1);
  not not_194 (not_194_out, OP0);
  not not_195 (not_195_out, F5);
  not not_196 (not_196_out, F4);
  not not_197 (not_197_out, F1);
  not not_198 (not_198_out, F0);
  not not_199 (not_199_out, OP5);
  not not_200 (not_200_out, OP4);
  not not_201 (not_201_out, OP2);
  not not_202 (not_202_out, OP1);
  not not_203 (not_203_out, OP0);
  not not_204 (not_204_out, OP5);
  not not_205 (not_205_out, OP4);
  not not_206 (not_206_out, OP2);
  not not_207 (not_207_out, OP1);
  not not_208 (not_208_out, OP5);
  not not_209 (not_209_out, OP4);
  not not_210 (not_210_out, OP2);
  not not_211 (not_211_out, OP0);
  not not_212 (not_212_out, OP4);
  not not_213 (not_213_out, OP3);
  not not_214 (not_214_out, OP2);
  not not_215 (not_215_out, OP4);
  not not_216 (not_216_out, OP2);
  not not_217 (not_217_out, OP4);
  not not_218 (not_218_out, OP2);
  not not_219 (not_219_out, OP1);
  not not_220 (not_220_out, OP0);
  not not_221 (not_221_out, OP5);
  not not_222 (not_222_out, OP4);
  not not_223 (not_223_out, OP3);
  not not_224 (not_224_out, OP2);
  not not_225 (not_225_out, OP1);
  not not_226 (not_226_out, OP0);
  not not_227 (not_227_out, F5);
  not not_228 (not_228_out, F4);
  not not_229 (not_229_out, F3);
  not not_230 (not_230_out, F2);
  not not_231 (not_231_out, F1);
  not not_232 (not_232_out, F0);
  not not_233 (not_233_out, OP5);
  not not_234 (not_234_out, OP4);
  not not_235 (not_235_out, OP3);
  not not_236 (not_236_out, OP2);
  not not_237 (not_237_out, OP1);
  not not_238 (not_238_out, OP0);
  not not_239 (not_239_out, F5);
  not not_240 (not_240_out, F4);
  not not_241 (not_241_out, F3);
  not not_242 (not_242_out, F2);
  not not_243 (not_243_out, OP5);
  not not_244 (not_244_out, OP4);
  not not_245 (not_245_out, OP3);
  not not_246 (not_246_out, OP2);
  not not_247 (not_247_out, OP1);
  not not_248 (not_248_out, OP0);
  not not_249 (not_249_out, F5);
  not not_250 (not_250_out, F4);
  not not_251 (not_251_out, F3);
  not not_252 (not_252_out, F2);
  not not_253 (not_253_out, F0);
  not not_254 (not_254_out, OP5);
  not not_255 (not_255_out, OP4);
  not not_256 (not_256_out, OP3);
  not not_257 (not_257_out, OP2);
  not not_258 (not_258_out, OP1);
  not not_259 (not_259_out, OP0);
  not not_260 (not_260_out, F4);
  not not_261 (not_261_out, F3);
  not not_262 (not_262_out, F2);
  not not_263 (not_263_out, F1);
  not not_264 (not_264_out, F0);
  not not_265 (not_265_out, OP5);
  not not_266 (not_266_out, OP4);
  not not_267 (not_267_out, OP3);
  not not_268 (not_268_out, OP2);
  not not_269 (not_269_out, OP1);
  not not_270 (not_270_out, OP0);
  not not_271 (not_271_out, F4);
  not not_272 (not_272_out, F3);
  not not_273 (not_273_out, F2);
  not not_274 (not_274_out, F1);
  not not_275 (not_275_out, OP5);
  not not_276 (not_276_out, OP4);
  not not_277 (not_277_out, OP3);
  not not_278 (not_278_out, OP2);
  not not_279 (not_279_out, OP1);
  not not_280 (not_280_out, OP0);
  not not_281 (not_281_out, F4);
  not not_282 (not_282_out, F3);
  not not_283 (not_283_out, F2);
  not not_284 (not_284_out, F0);
  not not_285 (not_285_out, OP5);
  not not_286 (not_286_out, OP4);
  not not_287 (not_287_out, OP3);
  not not_288 (not_288_out, OP2);
  not not_289 (not_289_out, OP1);
  not not_290 (not_290_out, OP0);
  not not_291 (not_291_out, F4);
  not not_292 (not_292_out, F3);
  not not_293 (not_293_out, F1);
  not not_294 (not_294_out, F0);
  not not_295 (not_295_out, OP5);
  not not_296 (not_296_out, OP4);
  not not_297 (not_297_out, OP3);
  not not_298 (not_298_out, OP2);
  not not_299 (not_299_out, OP1);
  not not_300 (not_300_out, OP0);
  not not_301 (not_301_out, F4);
  not not_302 (not_302_out, F3);
  not not_303 (not_303_out, F1);
  not not_304 (not_304_out, OP5);
  not not_305 (not_305_out, OP4);
  not not_306 (not_306_out, OP3);
  not not_307 (not_307_out, OP2);
  not not_308 (not_308_out, OP1);
  not not_309 (not_309_out, OP0);
  not not_310 (not_310_out, F4);
  not not_311 (not_311_out, F3);
  not not_312 (not_312_out, OP5);
  not not_313 (not_313_out, OP4);
  not not_314 (not_314_out, OP3);
  not not_315 (not_315_out, OP2);
  not not_316 (not_316_out, OP1);
  not not_317 (not_317_out, OP0);
  not not_318 (not_318_out, F4);
  not not_319 (not_319_out, F2);
  not not_320 (not_320_out, F0);
  not not_321 (not_321_out, OP5);
  not not_322 (not_322_out, OP4);
  not not_323 (not_323_out, OP3);
  not not_324 (not_324_out, OP2);
  not not_325 (not_325_out, OP1);
  not not_326 (not_326_out, OP0);
  not not_327 (not_327_out, F4);
  not not_328 (not_328_out, F2);
  not not_329 (not_329_out, OP5);
  not not_330 (not_330_out, OP4);
  not not_331 (not_331_out, OP3);
  not not_332 (not_332_out, OP2);
  not not_333 (not_333_out, OP1);
  not not_334 (not_334_out, OP0);
  not not_335 (not_335_out, F4);
  not not_336 (not_336_out, F3);
  not not_337 (not_337_out, F0);
  not not_338 (not_338_out, OP5);
  not not_339 (not_339_out, OP4);
  not not_340 (not_340_out, OP3);
  not not_341 (not_341_out, OP1);
  not not_342 (not_342_out, OP0);
  not not_343 (not_343_out, OP5);
  not not_344 (not_344_out, OP4);
  not not_345 (not_345_out, OP3);
  not not_346 (not_346_out, OP1);
  not not_347 (not_347_out, OP5);
  not not_348 (not_348_out, OP4);
  not not_349 (not_349_out, OP3);
  not not_350 (not_350_out, OP2);
  not not_351 (not_351_out, OP1);
  not not_352 (not_352_out, OP0);
  not not_353 (not_353_out, F5);
  not not_354 (not_354_out, F4);
  not not_355 (not_355_out, F2);
  not not_356 (not_356_out, F1);
  not not_357 (not_357_out, F0);
  not not_358 (not_358_out, OP5);
  not not_359 (not_359_out, OP4);
  not not_360 (not_360_out, OP3);
  not not_361 (not_361_out, OP2);
  not not_362 (not_362_out, OP1);
  not not_363 (not_363_out, OP0);
  not not_364 (not_364_out, F5);
  not not_365 (not_365_out, F4);
  not not_366 (not_366_out, F2);
  not not_367 (not_367_out, F1);
  not not_368 (not_368_out, F0);
  not not_369 (not_369_out, OP5);
  not not_370 (not_370_out, OP4);
  not not_371 (not_371_out, OP3);
  not not_372 (not_372_out, OP2);
  not not_373 (not_373_out, OP0);
  not not_374 (not_374_out, OP5);
  not not_375 (not_375_out, OP4);
  not not_376 (not_376_out, OP3);
  not not_377 (not_377_out, OP2);
  not not_378 (not_378_out, OP5);
  not not_379 (not_379_out, OP4);
  not not_380 (not_380_out, OP3);
  not not_381 (not_381_out, OP2);
  and and_1 (MemToReg, OP5, not_1_out, not_2_out, not_3_out, OP1, OP0);
  and and_2 (and_2_out, OP5, not_4_out, OP3, not_5_out, OP1, OP0);
  and and_3 (and_3_out, OP5, not_6_out, OP3, not_7_out, not_8_out, not_9_out);
  and and_4 (and_4_out, not_10_out, not_11_out, OP3, not_12_out, not_13_out, not_14_out);
  and and_5 (and_5_out, not_15_out, not_16_out, OP3, OP2, not_17_out, not_18_out);
  and and_6 (and_6_out, not_19_out, not_20_out, OP3, not_21_out, not_22_out, OP0);
  and and_7 (and_7_out, not_23_out, not_24_out, OP3, not_25_out, OP1, not_26_out);
  and and_8 (and_8_out, not_27_out, not_28_out, OP3, OP2, not_29_out, OP0);
  and and_9 (and_9_out, OP5, not_30_out, not_31_out, not_32_out, OP1, OP0);
  and and_10 (and_10_out, OP5, not_33_out, OP3, not_34_out, OP1, OP0);
  and and_11 (and_11_out, not_35_out, not_36_out, OP3, OP2, OP1, not_37_out);
  and and_12 (and_12_out, OP5, not_38_out, OP3, not_39_out, not_40_out, not_41_out);
  and and_13 (and_13_out, not_42_out, not_43_out, not_44_out, not_45_out, not_46_out, not_47_out, not_48_out, not_49_out, not_50_out, not_51_out, not_52_out, not_53_out);
  and and_14 (and_14_out, not_54_out, not_55_out, not_56_out, not_57_out, not_58_out, not_59_out, not_60_out, not_61_out, not_62_out, not_63_out, F1, F0);
  and and_15 (and_15_out, not_64_out, not_65_out, not_66_out, not_67_out, not_68_out, not_69_out, not_70_out, not_71_out, not_72_out, not_73_out, F1, not_74_out);
  and and_16 (and_16_out, not_75_out, not_76_out, not_77_out, not_78_out, not_79_out, not_80_out, F5, not_81_out, not_82_out, not_83_out, not_84_out, not_85_out);
  and and_17 (and_17_out, not_86_out, not_87_out, not_88_out, not_89_out, not_90_out, not_91_out, F5, not_92_out, not_93_out, not_94_out, not_95_out, F0);
  and and_18 (and_18_out, not_96_out, not_97_out, not_98_out, not_99_out, not_100_out, not_101_out, F5, not_102_out, not_103_out, not_104_out, F1, not_105_out);
  and and_19 (and_19_out, not_106_out, not_107_out, not_108_out, not_109_out, not_110_out, not_111_out, F5, not_112_out, not_113_out, F2, not_114_out, not_115_out);
  and and_20 (and_20_out, not_116_out, not_117_out, not_118_out, not_119_out, not_120_out, not_121_out, F5, not_122_out, not_123_out, F2, not_124_out, F0);
  and and_21 (and_21_out, not_125_out, not_126_out, not_127_out, not_128_out, not_129_out, not_130_out, F5, not_131_out, not_132_out, F2, F1, F0);
  and and_22 (and_22_out, not_133_out, not_134_out, not_135_out, not_136_out, not_137_out, not_138_out, F5, not_139_out, F3, not_140_out, F1, not_141_out);
  and and_23 (and_23_out, not_142_out, not_143_out, not_144_out, not_145_out, not_146_out, not_147_out, F5, not_148_out, F3, not_149_out, F1, F0);
  and and_24 (and_24_out, not_150_out, not_151_out, not_152_out, not_153_out, OP1, OP0);
  and and_25 (and_25_out, not_154_out, not_155_out, OP3, not_156_out, not_157_out, not_158_out);
  and and_26 (and_26_out, not_159_out, not_160_out, OP3, OP2, not_161_out, not_162_out);
  and and_27 (and_27_out, not_163_out, not_164_out, OP3, not_165_out, not_166_out, OP0);
  and and_28 (and_28_out, not_167_out, not_168_out, OP3, not_169_out, OP1, not_170_out);
  and and_29 (and_29_out, not_171_out, not_172_out, OP3, OP2, not_173_out, OP0);
  and and_30 (and_30_out, OP5, not_174_out, not_175_out, not_176_out, OP1, OP0);
  and and_31 (and_31_out, not_177_out, not_178_out, not_179_out, not_180_out, not_181_out, not_182_out, F5, not_183_out, not_184_out, F2, F1, not_185_out);
  and and_32 (and_32_out, not_186_out, not_187_out, OP3, OP2, OP1, not_188_out);
  and and_33 (SysCALL, not_189_out, not_190_out, not_191_out, not_192_out, not_193_out, not_194_out, not_195_out, not_196_out, F3, F2, not_197_out, not_198_out);
  and and_34 (and_34_out, not_199_out, not_200_out, OP3, not_201_out, not_202_out, not_203_out);
  and and_35 (and_35_out, not_204_out, not_205_out, OP3, not_206_out, not_207_out, OP0);
  and and_36 (and_36_out, not_208_out, not_209_out, OP3, not_210_out, OP1, not_211_out);
  and and_37 (and_37_out, OP5, not_212_out, not_213_out, not_214_out, OP1, OP0);
  and and_38 (and_38_out, OP5, not_215_out, OP3, not_216_out, OP1, OP0);
  and and_39 (and_39_out, OP5, not_217_out, OP3, not_218_out, not_219_out, not_220_out);
  and and_40 (and_40_out, not_221_out, not_222_out, not_223_out, not_224_out, not_225_out, not_226_out, not_227_out, not_228_out, not_229_out, not_230_out, not_231_out, not_232_out);
  and and_41 (and_41_out, not_233_out, not_234_out, not_235_out, not_236_out, not_237_out, not_238_out, not_239_out, not_240_out, not_241_out, not_242_out, F1, F0);
  and and_42 (and_42_out, not_243_out, not_244_out, not_245_out, not_246_out, not_247_out, not_248_out, not_249_out, not_250_out, not_251_out, not_252_out, F1, not_253_out);
  and and_43 (and_43_out, not_254_out, not_255_out, not_256_out, not_257_out, not_258_out, not_259_out, F5, not_260_out, not_261_out, not_262_out, not_263_out, not_264_out);
  and and_44 (and_44_out, not_265_out, not_266_out, not_267_out, not_268_out, not_269_out, not_270_out, F5, not_271_out, not_272_out, not_273_out, not_274_out, F0);
  and and_45 (and_45_out, not_275_out, not_276_out, not_277_out, not_278_out, not_279_out, not_280_out, F5, not_281_out, not_282_out, not_283_out, F1, not_284_out);
  and and_46 (and_46_out, not_285_out, not_286_out, not_287_out, not_288_out, not_289_out, not_290_out, F5, not_291_out, not_292_out, F2, not_293_out, not_294_out);
  and and_47 (and_47_out, not_295_out, not_296_out, not_297_out, not_298_out, not_299_out, not_300_out, F5, not_301_out, not_302_out, F2, not_303_out, F0);
  and and_48 (and_48_out, not_304_out, not_305_out, not_306_out, not_307_out, not_308_out, not_309_out, F5, not_310_out, not_311_out, F2, F1, F0);
  and and_49 (and_49_out, not_312_out, not_313_out, not_314_out, not_315_out, not_316_out, not_317_out, F5, not_318_out, F3, not_319_out, F1, not_320_out);
  and and_50 (and_50_out, not_321_out, not_322_out, not_323_out, not_324_out, not_325_out, not_326_out, F5, not_327_out, F3, not_328_out, F1, F0);
  and and_51 (and_51_out, not_329_out, not_330_out, not_331_out, not_332_out, not_333_out, not_334_out, F5, not_335_out, not_336_out, F2, F1, not_337_out);
  and and_52 (BEQ, not_338_out, not_339_out, not_340_out, OP2, not_341_out, not_342_out);
  and and_53 (BNE, not_343_out, not_344_out, not_345_out, OP2, not_346_out, OP0);
  and and_54 (JR, not_347_out, not_348_out, not_349_out, not_350_out, not_351_out, not_352_out, not_353_out, not_354_out, F3, not_355_out, not_356_out, not_357_out);
  and and_55 (and_55_out, not_358_out, not_359_out, not_360_out, not_361_out, not_362_out, not_363_out, not_364_out, not_365_out, F3, not_366_out, not_367_out, not_368_out);
  and and_56 (and_56_out, not_369_out, not_370_out, not_371_out, not_372_out, OP1, not_373_out);
  and and_57 (and_57_out, not_374_out, not_375_out, not_376_out, not_377_out, OP1, OP0);
  and and_58 (JAL, not_378_out, not_379_out, not_380_out, not_381_out, OP1, OP0);
  or or_1 (MemWrite, and_2_out, and_3_out);
  or or_2 (ALU_SRC, and_4_out, and_5_out, and_6_out, and_7_out, and_8_out, and_9_out, and_10_out, and_11_out, and_12_out);
  or or_3 (SignedExt, and_34_out, and_35_out, and_36_out, and_37_out, and_38_out, and_39_out);
  or or_4 (JMP, and_55_out, and_56_out, and_57_out);
  or or_5 (RegWrite, and_13_out, and_14_out, and_15_out, and_16_out, and_17_out, and_18_out, and_19_out, and_20_out, and_21_out, and_22_out, and_23_out, and_24_out, and_25_out, and_26_out, and_27_out, and_28_out, and_29_out, and_30_out, and_31_out, and_32_out);
  or or_6 (RegDst, and_40_out, and_41_out, and_42_out, and_43_out, and_44_out, and_45_out, and_46_out, and_47_out, and_48_out, and_49_out, and_50_out, and_51_out);
endmodule

module \附加控制信号  (
  input  OP0,
  input  OP1,
  input  OP2,
  input  OP3,
  input  OP4,
  input  OP5,
  output SB,
  output BLEZ
);

  wire not_1_out, not_2_out, not_3_out, not_4_out, not_5_out, not_6_out, not_7_out, not_8_out;

  not not_1 (not_1_out, OP4);
  not not_2 (not_2_out, OP2);
  not not_3 (not_3_out, OP1);
  not not_4 (not_4_out, OP0);
  not not_5 (not_5_out, OP5);
  not not_6 (not_6_out, OP4);
  not not_7 (not_7_out, OP3);
  not not_8 (not_8_out, OP0);
  and and_1 (SB, OP5, not_1_out, OP3, not_2_out, not_3_out, not_4_out);
  and and_2 (BLEZ, not_5_out, not_6_out, not_7_out, OP2, OP1, not_8_out);
endmodule

// ALU
module MIPS_ALU (
  input  [31:0] X,
  input  [31:0] Y,
  input  [3:0] AluOP,
  input  [4:0] shamt,
  output LEZ,
  output Equal,
  output [31:0] Result,
  output [31:0] Result_2
);

  wire comparator_3_eq, comparator_3_lt;
  wire [0:0] comparator_1_lt, comparator_2_lt;
  wire [31:0] adder_1_out, AND_out, divider_1_out, divider_1_rem, multiplier_1_cout, multiplier_1_out,
       NOR_out, OR_out, shifter_1_out, shifter_2_out, shifter_3_out, subtractor_1_out, XOR_out;

  assign AND_out = X & Y;  // AND_Gate AND, 32 bits wide
  assign OR_out = X | Y;  // OR_Gate OR, 32 bits wide
  Shifter #(.width(32)) shifter_1 (.in(Y), .\dist (shamt), .out(shifter_1_out));
  Shifter #(.width(32), .shift("ar")) shifter_2 (.in(Y), .\dist (shamt), .out(shifter_2_out));
  Shifter #(.width(32), .shift("lr")) shifter_3 (.in(Y), .\dist (shamt), .out(shifter_3_out));
  Multiplier #(.width(32)) multiplier_1 (.a(X), .b(Y), .out(multiplier_1_out), .cout(multiplier_1_cout));  // open: cin
  Divider #(.width(32)) divider_1 (.a(X), .b(Y), .out(divider_1_out), .rem(divider_1_rem));  // open: upper
  Adder #(.width(32)) adder_1 (.a(X), .b(Y), .out(adder_1_out));  // open: cin, cout
  Subtractor #(.width(32)) subtractor_1 (.a(X), .b(Y), .out(subtractor_1_out));  // open: bin, bout
  assign XOR_out = X ^ Y;  // XOR_Gate XOR, 32 bits wide
  assign NOR_out = ~(X | Y);  // NOR_Gate NOR, 32 bits wide
  Comparator #(.width(32)) comparator_1 (.a(X), .b(Y), .eq(Equal), .lt(comparator_1_lt[0]));  // open: gt
  Comparator #(.width(32), .mode("unsigned")) comparator_2 (.a(X), .b(Y), .lt(comparator_2_lt[0]));  // open: gt, eq
  Comparator #(.width(32)) comparator_3 (
    .a(X), .b({32{1'b0}}), .eq(comparator_3_eq), .lt(comparator_3_lt));  // open: gt
  or or_2 (LEZ, comparator_3_eq, comparator_3_lt);
  Multiplexer #(.select(4), .width(32), .enable("false")) multiplexer_1 (
    .in0(shifter_1_out), .in1(shifter_2_out), .in2(shifter_3_out), .in3(multiplier_1_out),
    .in4(divider_1_out), .in5(adder_1_out), .in6(subtractor_1_out), .in7(AND_out), .in8(OR_out),
    .in9(XOR_out), .in10(NOR_out), .in11({{31{1'b0}}, comparator_1_lt[0]}),
    .in12({{31{1'b0}}, comparator_2_lt[0]}), .in13({32{1'b0}}), .in14({32{1'b0}}), .in15({32{1'b0}}),
    .out(Result), .sel(AluOP));
  Multiplexer #(.select(4), .width(32), .enable("false")) multiplexer_2 (
    .in0({32{1'b0}}), .in1({32{1'b0}}), .in2({32{1'b0}}), .in3(multiplier_1_cout), .in4(divider_1_rem),
    .in5({32{1'b0}}), .in6({32{1'b0}}), .in7({32{1'b0}}), .in8({32{1'b0}}), .in9({32{1'b0}}),
    .in10({32{1'b0}}), .in11({32{1'b0}}), .in12({32{1'b0}}), .in13({32{1'b0}}), .in14({32{1'b0}}),
    .in15({32{1'b0}}), .out(Result_2), .sel(AluOP));

  // Other names for the same wires on the sheet: Result2[31:0] = Result_2; S[3:0] = AluOP

  // Notes on the sheet:
  //   不要改变此引脚区域内容，也不要改变ALU封装形式
  //   输入引脚
  //   输出引脚
endmodule

module MIPS_Regifile (
  input  [31:0] Din,
  input  Clk,
  input  WE,
  input  [4:0] R1_num,
  input  [4:0] W_num,
  input  [4:0] R2_num,
  output [31:0] R1,
  output [31:0] R2
);

  // RegisterFile registerfile_1: pin names not known; wires that end beside it: Din, Clk, WE, W_num, R1_num, R2_num, R1, R2
endmodule

module \IF_ID流水接口  (
  input  [31:0] PC_,
  input  [31:0] Inst,
  input  [31:0] PC,
  input  Pred,
  input  CLK,
  input  clr,
  input  EN,
  input  RST,
  output [31:0] PC__2,
  output [31:0] IR,
  output [31:0] PC_2,
  output Pred_2
);

  wire multiplexer_4_out;
  wire [31:0] multiplexer_1_out, multiplexer_2_out, multiplexer_3_out;

  Multiplexer #(.width(32), .enable("false")) multiplexer_1 (
    .in0(PC_), .in1({32{1'b0}}), .out(multiplexer_1_out), .sel(clr));
  Multiplexer #(.width(32), .enable("false")) multiplexer_2 (
    .in0(Inst), .in1({32{1'b0}}), .out(multiplexer_2_out), .sel(clr));
  Multiplexer #(.width(32), .enable("false")) multiplexer_3 (
    .in0(PC), .in1({32{1'b0}}), .out(multiplexer_3_out), .sel(clr));
  Multiplexer #(.enable("false")) multiplexer_4 (.in0(Pred), .in1(1'b0), .out(multiplexer_4_out), .sel(clr));
  Register #(.width(32)) u_PC_ (.D(multiplexer_1_out), .en(EN), .Q(PC__2), .clk(CLK), .clr(RST));
  Register #(.width(32)) u_IR (.D(multiplexer_2_out), .en(EN), .Q(IR), .clk(CLK), .clr(RST));
  Register #(.width(32)) u_PC (.D(multiplexer_3_out), .en(EN), .Q(PC_2), .clk(CLK), .clr(RST));
  Register #(.width(1)) u_Pred (.D(multiplexer_4_out), .en(EN), .Q(Pred_2), .clk(CLK), .clr(RST));
endmodule

module \ID_EX流水接口  (
  input  RegWrite,
  input  RegDst,
  input  JAL,
  input  SB,
  input  MemToReg,
  input  MemWrite,
  input  [3:0] AluOp,
  input  AluSrcB,
  input  SignedExt,
  input  Halt,
  input  JMP,
  input  JR,
  input  Beq,
  input  Bne,
  input  Blez,
  input  [31:0] IR,
  input  [31:0] PC,
  input  [31:0] A,
  input  [31:0] B,
  input  [31:0] Imm,
  input  [31:0] PC_,
  input  Pred,
  input  CLK,
  input  clr,
  input  EN,
  input  RST,
  output RegWrite_2,
  output RegDst_2,
  output JAL_2,
  output SB_2,
  output MemToReg_2,
  output MemWrite_2,
  output [3:0] AluOp_2,
  output AluSrcB_2,
  output SignedExt_2,
  output Halt_2,
  output JMP_2,
  output JR_2,
  output Beq_2,
  output Bne_2,
  output Blez_2,
  output [31:0] IR_2,
  output [31:0] PC_2,
  output [31:0] A_2,
  output [31:0] B_2,
  output [31:0] Imm_2,
  output [31:0] PC__2,
  output Pred_2
);

  wire multiplexer_10_out;
  wire [2:0] multiplexer_1_out, multiplexer_2_out;
  wire [11:0] multiplexer_3_out;
  wire [31:0] multiplexer_4_out, multiplexer_5_out, multiplexer_6_out, multiplexer_7_out, multiplexer_8_out,
       multiplexer_9_out;

  Multiplexer #(.width(3), .enable("false")) multiplexer_1 (
    .in0({JAL, RegDst, RegWrite}), .in1(3'b000), .out(multiplexer_1_out), .sel(clr));
  Multiplexer #(.width(3), .enable("false")) multiplexer_2 (
    .in0({MemWrite, MemToReg, SB}), .in1(3'b000), .out(multiplexer_2_out), .sel(clr));
  Multiplexer #(.width(12), .enable("false")) multiplexer_3 (
    .in0({Blez, Bne, Beq, JR, JMP, Halt, SignedExt, AluSrcB, AluOp}), .in1({12{1'b0}}),
    .out(multiplexer_3_out), .sel(clr));
  Multiplexer #(.width(32), .enable("false")) multiplexer_4 (
    .in0(IR), .in1({32{1'b0}}), .out(multiplexer_4_out), .sel(clr));
  Multiplexer #(.width(32), .enable("false")) multiplexer_5 (
    .in0(PC), .in1({32{1'b0}}), .out(multiplexer_5_out), .sel(clr));
  Multiplexer #(.width(32), .enable("false")) multiplexer_6 (
    .in0(A), .in1({32{1'b0}}), .out(multiplexer_6_out), .sel(clr));
  Multiplexer #(.width(32), .enable("false")) multiplexer_7 (
    .in0(B), .in1({32{1'b0}}), .out(multiplexer_7_out), .sel(clr));
  Multiplexer #(.width(32), .enable("false")) multiplexer_8 (
    .in0(Imm), .in1({32{1'b0}}), .out(multiplexer_8_out), .sel(clr));
  Multiplexer #(.width(32), .enable("false")) multiplexer_9 (
    .in0(PC_), .in1({32{1'b0}}), .out(multiplexer_9_out), .sel(clr));
  Multiplexer #(.enable("false")) multiplexer_10 (.in0(Pred), .in1(1'b0), .out(multiplexer_10_out), .sel(clr));
  Register #(.width(3)) WB (.D(multiplexer_1_out), .en(EN), .Q({JAL_2, RegDst_2, RegWrite_2}), .clk(CLK), .clr(RST));
  Register #(.width(3)) MEM (.D(multiplexer_2_out), .en(EN), .Q({MemWrite_2, MemToReg_2, SB_2}), .clk(CLK), .clr(RST));
  Register #(.width(12)) EX (
    .D(multiplexer_3_out), .en(EN),
    .Q({Blez_2, Bne_2, Beq_2, JR_2, JMP_2, Halt_2, SignedExt_2, AluSrcB_2, AluOp_2}), .clk(CLK), .clr(RST));
  Register #(.width(32)) u_IR (.D(multiplexer_4_out), .en(EN), .Q(IR_2), .clk(CLK), .clr(RST));
  Register #(.width(32)) u_PC (.D(multiplexer_5_out), .en(EN), .Q(PC_2), .clk(CLK), .clr(RST));
  Register #(.width(32)) u_A (.D(multiplexer_6_out), .en(EN), .Q(A_2), .clk(CLK), .clr(RST));
  Register #(.width(32)) u_B (.D(multiplexer_7_out), .en(EN), .Q(B_2), .clk(CLK), .clr(RST));
  Register #(.width(32)) u_Imm (.D(multiplexer_8_out), .en(EN), .Q(Imm_2), .clk(CLK), .clr(RST));
  Register #(.width(32)) u_PC_ (.D(multiplexer_9_out), .en(EN), .Q(PC__2), .clk(CLK), .clr(RST));
  Register #(.width(1)) u_Pred (.D(multiplexer_10_out), .en(EN), .Q(Pred_2), .clk(CLK), .clr(RST));
endmodule

module \EX_MEM流水接口  (
  input  Halt,
  input  RegWrite,
  input  RegDst,
  input  JAL,
  input  SB,
  input  MemToReg,
  input  MemWrite,
  input  [31:0] IR,
  input  [31:0] PC,
  input  [31:0] ALU,
  input  [31:0] B,
  input  CLK,
  input  clr,
  input  EN,
  input  RST,
  output Halt_2,
  output RegWrite_2,
  output RegDst_2,
  output JAL_2,
  output SB_2,
  output MemToReg_2,
  output MemWrite_2,
  output [31:0] IR_2,
  output [31:0] PC_2,
  output [31:0] ALU_2,
  output [31:0] B_2
);

  wire multiplexer_1_out;
  wire [2:0] multiplexer_2_out, multiplexer_3_out;
  wire [31:0] multiplexer_4_out, multiplexer_5_out, multiplexer_6_out, multiplexer_7_out;

  Multiplexer #(.enable("false")) multiplexer_1 (.in0(Halt), .in1(1'b0), .out(multiplexer_1_out), .sel(clr));
  Multiplexer #(.width(3), .enable("false")) multiplexer_2 (
    .in0({JAL, RegDst, RegWrite}), .in1(3'b000), .out(multiplexer_2_out), .sel(clr));
  Multiplexer #(.width(3), .enable("false")) multiplexer_3 (
    .in0({MemWrite, MemToReg, SB}), .in1(3'b000), .out(multiplexer_3_out), .sel(clr));
  Multiplexer #(.width(32), .enable("false")) multiplexer_4 (
    .in0(IR), .in1({32{1'b0}}), .out(multiplexer_4_out), .sel(clr));
  Multiplexer #(.width(32), .enable("false")) multiplexer_5 (
    .in0(PC), .in1({32{1'b0}}), .out(multiplexer_5_out), .sel(clr));
  Multiplexer #(.width(32), .enable("false")) multiplexer_6 (
    .in0(ALU), .in1({32{1'b0}}), .out(multiplexer_6_out), .sel(clr));
  Multiplexer #(.width(32), .enable("false")) multiplexer_7 (
    .in0(B), .in1({32{1'b0}}), .out(multiplexer_7_out), .sel(clr));
  Register #(.width(1)) sys (.D(multiplexer_1_out), .en(EN), .Q(Halt_2), .clk(CLK), .clr(RST));
  Register #(.width(3)) WB (.D(multiplexer_2_out), .en(EN), .Q({JAL_2, RegDst_2, RegWrite_2}), .clk(CLK), .clr(RST));
  Register #(.width(3)) MEM (.D(multiplexer_3_out), .en(EN), .Q({MemWrite_2, MemToReg_2, SB_2}), .clk(CLK), .clr(RST));
  Register #(.width(32)) u_IR (.D(multiplexer_4_out), .en(EN), .Q(IR_2), .clk(CLK), .clr(RST));
  Register #(.width(32)) u_PC (.D(multiplexer_5_out), .en(EN), .Q(PC_2), .clk(CLK), .clr(RST));
  Register #(.width(32)) u_ALU (.D(multiplexer_6_out), .en(EN), .Q(ALU_2), .clk(CLK), .clr(RST));
  Register #(.width(32)) u_B (.D(multiplexer_7_out), .en(EN), .Q(B_2), .clk(CLK), .clr(RST));
endmodule

module \MEM_WB流水接口  (
  input  Halt,
  input  RegWrite,
  input  RegDst,
  input  JAL,
  input  [31:0] IR,
  input  [31:0] PC,
  input  [31:0] ALU,
  input  [31:0] MD,
  input  CLK,
  input  clr,
  input  EN,
  input  RST,
  output Halt_2,
  output RegWrite_2,
  output RegDst_2,
  output JAL_2,
  output [31:0] IR_2,
  output [31:0] PC_2,
  output [31:0] ALU_2,
  output [31:0] MD_2
);

  wire multiplexer_1_out;
  wire [2:0] multiplexer_2_out;
  wire [31:0] multiplexer_3_out, multiplexer_4_out, multiplexer_5_out, multiplexer_6_out;

  Multiplexer #(.enable("false")) multiplexer_1 (.in0(Halt), .in1(1'b0), .out(multiplexer_1_out), .sel(clr));
  Multiplexer #(.width(3), .enable("false")) multiplexer_2 (
    .in0({JAL, RegDst, RegWrite}), .in1(3'b000), .out(multiplexer_2_out), .sel(clr));
  Multiplexer #(.width(32), .enable("false")) multiplexer_3 (
    .in0(IR), .in1({32{1'b0}}), .out(multiplexer_3_out), .sel(clr));
  Multiplexer #(.width(32), .enable("false")) multiplexer_4 (
    .in0(PC), .in1({32{1'b0}}), .out(multiplexer_4_out), .sel(clr));
  Multiplexer #(.width(32), .enable("false")) multiplexer_5 (
    .in0(ALU), .in1({32{1'b0}}), .out(multiplexer_5_out), .sel(clr));
  Multiplexer #(.width(32), .enable("false")) multiplexer_6 (
    .in0(MD), .in1({32{1'b0}}), .out(multiplexer_6_out), .sel(clr));
  Register #(.width(1)) sys (.D(multiplexer_1_out), .en(EN), .Q(Halt_2), .clk(CLK), .clr(RST));
  Register #(.width(3)) WB (.D(multiplexer_2_out), .en(EN), .Q({JAL_2, RegDst_2, RegWrite_2}), .clk(CLK), .clr(RST));
  Register #(.width(32)) u_IR (.D(multiplexer_3_out), .en(EN), .Q(IR_2), .clk(CLK), .clr(RST));
  Register #(.width(32)) u_PC (.D(multiplexer_4_out), .en(EN), .Q(PC_2), .clk(CLK), .clr(RST));
  Register #(.width(32)) u_ALU (.D(multiplexer_5_out), .en(EN), .Q(ALU_2), .clk(CLK), .clr(RST));
  Register #(.width(32)) u_MD (.D(multiplexer_6_out), .en(EN), .Q(MD_2), .clk(CLK), .clr(RST));
endmodule
module \源寄存器使用情况  (
  input  OP0,
  input  OP1,
  input  OP2,
  input  OP3,
  input  OP4,
  input  OP5,
  input  F0,
  input  F1,
  input  F2,
  input  F3,
  input  F4,
  input  F5,
  output R1_Used,
  output R2_Used
);

  wire and_1_out, and_2_out, and_3_out, and_4_out, and_5_out, and_6_out, and_7_out, and_8_out, and_9_out,
       and_10_out, and_11_out, and_12_out, and_13_out, and_14_out, and_15_out, and_16_out, and_17_out,
       and_18_out, and_19_out, and_20_out, and_21_out, and_22_out, and_23_out, and_24_out, and_25_out,
       and_26_out, and_27_out, and_28_out, and_29_out, and_30_out, and_31_out, and_32_out, and_33_out,
       and_34_out, and_35_out, and_36_out, and_37_out, and_38_out, not_1_out, not_2_out, not_3_out,
       not_4_out, not_5_out, not_6_out, not_7_out, not_8_out, not_9_out, not_10_out, not_11_out, not_12_out,
       not_13_out, not_14_out, not_15_out, not_16_out, not_17_out, not_18_out, not_19_out, not_20_out,
       not_21_out, not_22_out, not_23_out, not_24_out, not_25_out, not_26_out, not_27_out, not_28_out,
       not_29_out, not_30_out, not_31_out, not_32_out, not_33_out, not_34_out, not_35_out, not_36_out,
       not_37_out, not_38_out, not_39_out, not_40_out, not_41_out, not_42_out, not_43_out, not_44_out,
       not_45_out, not_46_out, not_47_out, not_48_out, not_49_out, not_50_out, not_51_out, not_52_out,
       not_53_out, not_54_out, not_55_out, not_56_out, not_57_out, not_58_out, not_59_out, not_60_out,
       not_61_out, not_62_out, not_63_out, not_64_out, not_65_out, not_66_out, not_67_out, not_68_out,
       not_69_out, not_70_out, not_71_out, not_72_out, not_73_out, not_74_out, not_75_out, not_76_out,
       not_77_out, not_78_out, not_79_out, not_80_out, not_81_out, not_82_out, not_83_out, not_84_out,
       not_85_out, not_86_out, not_87_out, not_88_out, not_89_out, not_90_out, not_91_out, not_92_out,
       not_93_out, not_94_out, not_95_out, not_96_out, not_97_out, not_98_out, not_99_out, not_100_out,
       not_101_out, not_102_out, not_103_out, not_104_out, not_105_out, not_106_out, not_107_out,
       not_108_out, not_109_out, not_110_out, not_111_out, not_112_out, not_113_out, not_114_out,
       not_115_out, not_116_out, not_117_out, not_118_out, not_119_out, not_120_out, not_121_out,
       not_122_out, not_123_out, not_124_out, not_125_out, not_126_out, not_127_out, not_128_out,
       not_129_out, not_130_out, not_131_out, not_132_out, not_133_out, not_134_out, not_135_out,
       not_136_out, not_137_out, not_138_out, not_139_out, not_140_out, not_141_out, not_142_out,
       not_143_out, not_144_out, not_145_out, not_146_out, not_147_out, not_148_out, not_149_out,
       not_150_out, not_151_out, not_152_out, not_153_out, not_154_out, not_155_out, not_156_out,
       not_157_out, not_158_out, not_159_out, not_160_out, not_161_out, not_162_out, not_163_out,
       not_164_out, not_165_out, not_166_out, not_167_out, not_168_out, not_169_out, not_170_out,
       not_171_out, not_172_out, not_173_out, not_174_out, not_175_out, not_176_out, not_177_out,
       not_178_out, not_179_out, not_180_out, not_181_out, not_182_out, not_183_out, not_184_out,
       not_185_out, not_186_out, not_187_out, not_188_out, not_189_out, not_190_out, not_191_out,
       not_192_out, not_193_out, not_194_out, not_195_out, not_196_out, not_197_out, not_198_out,
       not_199_out, not_200_out, not_201_out, not_202_out, not_203_out, not_204_out, not_205_out,
       not_206_out, not_207_out, not_208_out, not_209_out, not_210_out, not_211_out, not_212_out,
       not_213_out, not_214_out, not_215_out, not_216_out, not_217_out, not_218_out, not_219_out,
       not_220_out, not_221_out, not_222_out, not_223_out, not_224_out, not_225_out, not_226_out,
       not_227_out, not_228_out, not_229_out, not_230_out, not_231_out, not_232_out, not_233_out,
       not_234_out, not_235_out, not_236_out, not_237_out, not_238_out, not_239_out, not_240_out,
       not_241_out, not_242_out, not_243_out, not_244_out, not_245_out, not_246_out, not_247_out,
       not_248_out, not_249_out, not_250_out, not_251_out, not_252_out, not_253_out, not_254_out,
       not_255_out, not_256_out, not_257_out, not_258_out, not_259_out, not_260_out, not_261_out,
       not_262_out, not_263_out, not_264_out, not_265_out, not_266_out, not_267_out, not_268_out,
       not_269_out, not_270_out, not_271_out, not_272_out, not_273_out, not_274_out, not_275_out,
       not_276_out, not_277_out, not_278_out, not_279_out, not_280_out, not_281_out, not_282_out,
       not_283_out, not_284_out, not_285_out, not_286_out;

  not not_1 (not_1_out, OP5);
  not not_2 (not_2_out, OP4);
  not not_3 (not_3_out, OP3);
  not not_4 (not_4_out, OP2);
  not not_5 (not_5_out, OP1);
  not not_6 (not_6_out, OP0);
  not not_7 (not_7_out, F4);
  not not_8 (not_8_out, F3);
  not not_9 (not_9_out, F2);
  not not_10 (not_10_out, F1);
  not not_11 (not_11_out, F0);
  not not_12 (not_12_out, OP5);
  not not_13 (not_13_out, OP4);
  not not_14 (not_14_out, OP3);
  not not_15 (not_15_out, OP2);
  not not_16 (not_16_out, OP1);
  not not_17 (not_17_out, OP0);
  not not_18 (not_18_out, F4);
  not not_19 (not_19_out, F3);
  not not_20 (not_20_out, F2);
  not not_21 (not_21_out, F1);
  not not_22 (not_22_out, OP5);
  not not_23 (not_23_out, OP4);
  not not_24 (not_24_out, OP3);
  not not_25 (not_25_out, OP2);
  not not_26 (not_26_out, OP1);
  not not_27 (not_27_out, OP0);
  not not_28 (not_28_out, F4);
  not not_29 (not_29_out, F3);
  not not_30 (not_30_out, F2);
  not not_31 (not_31_out, F0);
  not not_32 (not_32_out, OP5);
  not not_33 (not_33_out, OP4);
  not not_34 (not_34_out, OP3);
  not not_35 (not_35_out, OP2);
  not not_36 (not_36_out, OP1);
  not not_37 (not_37_out, OP0);
  not not_38 (not_38_out, F4);
  not not_39 (not_39_out, F3);
  not not_40 (not_40_out, F1);
  not not_41 (not_41_out, F0);
  not not_42 (not_42_out, OP5);
  not not_43 (not_43_out, OP4);
  not not_44 (not_44_out, OP3);
  not not_45 (not_45_out, OP2);
  not not_46 (not_46_out, OP1);
  not not_47 (not_47_out, OP0);
  not not_48 (not_48_out, F4);
  not not_49 (not_49_out, F3);
  not not_50 (not_50_out, F1);
  not not_51 (not_51_out, OP5);
  not not_52 (not_52_out, OP4);
  not not_53 (not_53_out, OP3);
  not not_54 (not_54_out, OP2);
  not not_55 (not_55_out, OP1);
  not not_56 (not_56_out, OP0);
  not not_57 (not_57_out, F4);
  not not_58 (not_58_out, F3);
  not not_59 (not_59_out, OP5);
  not not_60 (not_60_out, OP4);
  not not_61 (not_61_out, OP3);
  not not_62 (not_62_out, OP2);
  not not_63 (not_63_out, OP1);
  not not_64 (not_64_out, OP0);
  not not_65 (not_65_out, F4);
  not not_66 (not_66_out, F2);
  not not_67 (not_67_out, F0);
  not not_68 (not_68_out, OP5);
  not not_69 (not_69_out, OP4);
  not not_70 (not_70_out, OP3);
  not not_71 (not_71_out, OP2);
  not not_72 (not_72_out, OP1);
  not not_73 (not_73_out, OP0);
  not not_74 (not_74_out, F4);
  not not_75 (not_75_out, F2);
  not not_76 (not_76_out, OP5);
  not not_77 (not_77_out, OP4);
  not not_78 (not_78_out, OP3);
  not not_79 (not_79_out, OP2);
  not not_80 (not_80_out, OP1);
  not not_81 (not_81_out, OP0);
  not not_82 (not_82_out, F5);
  not not_83 (not_83_out, F4);
  not not_84 (not_84_out, F2);
  not not_85 (not_85_out, F1);
  not not_86 (not_86_out, F0);
  not not_87 (not_87_out, OP5);
  not not_88 (not_88_out, OP4);
  not not_89 (not_89_out, OP3);
  not not_90 (not_90_out, OP2);
  not not_91 (not_91_out, OP1);
  not not_92 (not_92_out, OP0);
  not not_93 (not_93_out, F5);
  not not_94 (not_94_out, F4);
  not not_95 (not_95_out, F1);
  not not_96 (not_96_out, F0);
  not not_97 (not_97_out, OP5);
  not not_98 (not_98_out, OP4);
  not not_99 (not_99_out, OP3);
  not not_100 (not_100_out, OP1);
  not not_101 (not_101_out, OP0);
  not not_102 (not_102_out, OP5);
  not not_103 (not_103_out, OP4);
  not not_104 (not_104_out, OP3);
  not not_105 (not_105_out, OP1);
  not not_106 (not_106_out, OP5);
  not not_107 (not_107_out, OP4);
  not not_108 (not_108_out, OP2);
  not not_109 (not_109_out, OP1);
  not not_110 (not_110_out, OP0);
  not not_111 (not_111_out, OP5);
  not not_112 (not_112_out, OP4);
  not not_113 (not_113_out, OP1);
  not not_114 (not_114_out, OP0);
  not not_115 (not_115_out, OP5);
  not not_116 (not_116_out, OP4);
  not not_117 (not_117_out, OP2);
  not not_118 (not_118_out, OP1);
  not not_119 (not_119_out, OP5);
  not not_120 (not_120_out, OP4);
  not not_121 (not_121_out, OP2);
  not not_122 (not_122_out, OP0);
  not not_123 (not_123_out, OP5);
  not not_124 (not_124_out, OP4);
  not not_125 (not_125_out, OP1);
  not not_126 (not_126_out, OP4);
  not not_127 (not_127_out, OP3);
  not not_128 (not_128_out, OP2);
  not not_129 (not_129_out, OP4);
  not not_130 (not_130_out, OP2);
  not not_131 (not_131_out, OP5);
  not not_132 (not_132_out, OP4);
  not not_133 (not_133_out, OP3);
  not not_134 (not_134_out, OP2);
  not not_135 (not_135_out, OP1);
  not not_136 (not_136_out, OP0);
  not not_137 (not_137_out, F4);
  not not_138 (not_138_out, F3);
  not not_139 (not_139_out, F0);
  not not_140 (not_140_out, OP5);
  not not_141 (not_141_out, OP4);
  not not_142 (not_142_out, OP0);
  not not_143 (not_143_out, OP4);
  not not_144 (not_144_out, OP2);
  not not_145 (not_145_out, OP1);
  not not_146 (not_146_out, OP0);
  not not_147 (not_147_out, OP5);
  not not_148 (not_148_out, OP4);
  not not_149 (not_149_out, OP3);
  not not_150 (not_150_out, OP0);
  not not_151 (not_151_out, OP5);
  not not_152 (not_152_out, OP4);
  not not_153 (not_153_out, OP3);
  not not_154 (not_154_out, OP2);
  not not_155 (not_155_out, OP1);
  not not_156 (not_156_out, OP0);
  not not_157 (not_157_out, F5);
  not not_158 (not_158_out, F4);
  not not_159 (not_159_out, F3);
  not not_160 (not_160_out, F2);
  not not_161 (not_161_out, F1);
  not not_162 (not_162_out, F0);
  not not_163 (not_163_out, OP5);
  not not_164 (not_164_out, OP4);
  not not_165 (not_165_out, OP3);
  not not_166 (not_166_out, OP2);
  not not_167 (not_167_out, OP1);
  not not_168 (not_168_out, OP0);
  not not_169 (not_169_out, F5);
  not not_170 (not_170_out, F4);
  not not_171 (not_171_out, F3);
  not not_172 (not_172_out, F2);
  not not_173 (not_173_out, OP5);
  not not_174 (not_174_out, OP4);
  not not_175 (not_175_out, OP3);
  not not_176 (not_176_out, OP2);
  not not_177 (not_177_out, OP1);
  not not_178 (not_178_out, OP0);
  not not_179 (not_179_out, F5);
  not not_180 (not_180_out, F4);
  not not_181 (not_181_out, F3);
  not not_182 (not_182_out, F2);
  not not_183 (not_183_out, F0);
  not not_184 (not_184_out, OP5);
  not not_185 (not_185_out, OP4);
  not not_186 (not_186_out, OP3);
  not not_187 (not_187_out, OP2);
  not not_188 (not_188_out, OP1);
  not not_189 (not_189_out, OP0);
  not not_190 (not_190_out, F4);
  not not_191 (not_191_out, F3);
  not not_192 (not_192_out, F2);
  not not_193 (not_193_out, F1);
  not not_194 (not_194_out, F0);
  not not_195 (not_195_out, OP5);
  not not_196 (not_196_out, OP4);
  not not_197 (not_197_out, OP3);
  not not_198 (not_198_out, OP2);
  not not_199 (not_199_out, OP1);
  not not_200 (not_200_out, OP0);
  not not_201 (not_201_out, F4);
  not not_202 (not_202_out, F3);
  not not_203 (not_203_out, F2);
  not not_204 (not_204_out, F1);
  not not_205 (not_205_out, OP5);
  not not_206 (not_206_out, OP4);
  not not_207 (not_207_out, OP3);
  not not_208 (not_208_out, OP2);
  not not_209 (not_209_out, OP1);
  not not_210 (not_210_out, OP0);
  not not_211 (not_211_out, F4);
  not not_212 (not_212_out, F3);
  not not_213 (not_213_out, F2);
  not not_214 (not_214_out, F0);
  not not_215 (not_215_out, OP5);
  not not_216 (not_216_out, OP4);
  not not_217 (not_217_out, OP3);
  not not_218 (not_218_out, OP2);
  not not_219 (not_219_out, OP1);
  not not_220 (not_220_out, OP0);
  not not_221 (not_221_out, F4);
  not not_222 (not_222_out, F3);
  not not_223 (not_223_out, F1);
  not not_224 (not_224_out, F0);
  not not_225 (not_225_out, OP5);
  not not_226 (not_226_out, OP4);
  not not_227 (not_227_out, OP3);
  not not_228 (not_228_out, OP2);
  not not_229 (not_229_out, OP1);
  not not_230 (not_230_out, OP0);
  not not_231 (not_231_out, F4);
  not not_232 (not_232_out, F3);
  not not_233 (not_233_out, F1);
  not not_234 (not_234_out, OP5);
  not not_235 (not_235_out, OP4);
  not not_236 (not_236_out, OP3);
  not not_237 (not_237_out, OP2);
  not not_238 (not_238_out, OP1);
  not not_239 (not_239_out, OP0);
  not not_240 (not_240_out, F4);
  not not_241 (not_241_out, F3);
  not not_242 (not_242_out, OP5);
  not not_243 (not_243_out, OP4);
  not not_244 (not_244_out, OP3);
  not not_245 (not_245_out, OP2);
  not not_246 (not_246_out, OP1);
  not not_247 (not_247_out, OP0);
  not not_248 (not_248_out, F4);
  not not_249 (not_249_out, F2);
  not not_250 (not_250_out, F0);
  not not_251 (not_251_out, OP5);
  not not_252 (not_252_out, OP4);
  not not_253 (not_253_out, OP3);
  not not_254 (not_254_out, OP2);
  not not_255 (not_255_out, OP1);
  not not_256 (not_256_out, OP0);
  not not_257 (not_257_out, F4);
  not not_258 (not_258_out, F2);
  not not_259 (not_259_out, OP5);
  not not_260 (not_260_out, OP4);
  not not_261 (not_261_out, OP3);
  not not_262 (not_262_out, OP2);
  not not_263 (not_263_out, OP1);
  not not_264 (not_264_out, OP0);
  not not_265 (not_265_out, F5);
  not not_266 (not_266_out, F4);
  not not_267 (not_267_out, F1);
  not not_268 (not_268_out, F0);
  not not_269 (not_269_out, OP5);
  not not_270 (not_270_out, OP4);
  not not_271 (not_271_out, OP3);
  not not_272 (not_272_out, OP1);
  not not_273 (not_273_out, OP0);
  not not_274 (not_274_out, OP5);
  not not_275 (not_275_out, OP4);
  not not_276 (not_276_out, OP3);
  not not_277 (not_277_out, OP1);
  not not_278 (not_278_out, OP5);
  not not_279 (not_279_out, OP4);
  not not_280 (not_280_out, OP3);
  not not_281 (not_281_out, OP2);
  not not_282 (not_282_out, OP1);
  not not_283 (not_283_out, OP0);
  not not_284 (not_284_out, F4);
  not not_285 (not_285_out, F3);
  not not_286 (not_286_out, F0);
  and and_1 (and_1_out, not_1_out, not_2_out, not_3_out, not_4_out, not_5_out, not_6_out, F5, not_7_out, not_8_out, not_9_out, not_10_out, not_11_out);
  and and_2 (and_2_out, not_12_out, not_13_out, not_14_out, not_15_out, not_16_out, not_17_out, F5, not_18_out, not_19_out, not_20_out, not_21_out, F0);
  and and_3 (and_3_out, not_22_out, not_23_out, not_24_out, not_25_out, not_26_out, not_27_out, F5, not_28_out, not_29_out, not_30_out, F1, not_31_out);
  and and_4 (and_4_out, not_32_out, not_33_out, not_34_out, not_35_out, not_36_out, not_37_out, F5, not_38_out, not_39_out, F2, not_40_out, not_41_out);
  and and_5 (and_5_out, not_42_out, not_43_out, not_44_out, not_45_out, not_46_out, not_47_out, F5, not_48_out, not_49_out, F2, not_50_out, F0);
  and and_6 (and_6_out, not_51_out, not_52_out, not_53_out, not_54_out, not_55_out, not_56_out, F5, not_57_out, not_58_out, F2, F1, F0);
  and and_7 (and_7_out, not_59_out, not_60_out, not_61_out, not_62_out, not_63_out, not_64_out, F5, not_65_out, F3, not_66_out, F1, not_67_out);
  and and_8 (and_8_out, not_68_out, not_69_out, not_70_out, not_71_out, not_72_out, not_73_out, F5, not_74_out, F3, not_75_out, F1, F0);
  and and_9 (and_9_out, not_76_out, not_77_out, not_78_out, not_79_out, not_80_out, not_81_out, not_82_out, not_83_out, F3, not_84_out, not_85_out, not_86_out);
  and and_10 (and_10_out, not_87_out, not_88_out, not_89_out, not_90_out, not_91_out, not_92_out, not_93_out, not_94_out, F3, F2, not_95_out, not_96_out);
  and and_11 (and_11_out, not_97_out, not_98_out, not_99_out, OP2, not_100_out, not_101_out);
  and and_12 (and_12_out, not_102_out, not_103_out, not_104_out, OP2, not_105_out, OP0);
  and and_13 (and_13_out, not_106_out, not_107_out, OP3, not_108_out, not_109_out, not_110_out);
  and and_14 (and_14_out, not_111_out, not_112_out, OP3, OP2, not_113_out, not_114_out);
  and and_15 (and_15_out, not_115_out, not_116_out, OP3, not_117_out, not_118_out, OP0);
  and and_16 (and_16_out, not_119_out, not_120_out, OP3, not_121_out, OP1, not_122_out);
  and and_17 (and_17_out, not_123_out, not_124_out, OP3, OP2, not_125_out, OP0);
  and and_18 (and_18_out, OP5, not_126_out, not_127_out, not_128_out, OP1, OP0);
  and and_19 (and_19_out, OP5, not_129_out, OP3, not_130_out, OP1, OP0);
  and and_20 (and_20_out, not_131_out, not_132_out, not_133_out, not_134_out, not_135_out, not_136_out, F5, not_137_out, not_138_out, F2, F1, not_139_out);
  and and_21 (and_21_out, not_140_out, not_141_out, OP3, OP2, OP1, not_142_out);
  and and_22 (and_22_out, OP5, not_143_out, OP3, not_144_out, not_145_out, not_146_out);
  and and_23 (and_23_out, not_147_out, not_148_out, not_149_out, OP2, OP1, not_150_out);
  and and_24 (and_24_out, not_151_out, not_152_out, not_153_out, not_154_out, not_155_out, not_156_out, not_157_out, not_158_out, not_159_out, not_160_out, not_161_out, not_162_out);
  and and_25 (and_25_out, not_163_out, not_164_out, not_165_out, not_166_out, not_167_out, not_168_out, not_169_out, not_170_out, not_171_out, not_172_out, F1, F0);
  and and_26 (and_26_out, not_173_out, not_174_out, not_175_out, not_176_out, not_177_out, not_178_out, not_179_out, not_180_out, not_181_out, not_182_out, F1, not_183_out);
  and and_27 (and_27_out, not_184_out, not_185_out, not_186_out, not_187_out, not_188_out, not_189_out, F5, not_190_out, not_191_out, not_192_out, not_193_out, not_194_out);
  and and_28 (and_28_out, not_195_out, not_196_out, not_197_out, not_198_out, not_199_out, not_200_out, F5, not_201_out, not_202_out, not_203_out, not_204_out, F0);
  and and_29 (and_29_out, not_205_out, not_206_out, not_207_out, not_208_out, not_209_out, not_210_out, F5, not_211_out, not_212_out, not_213_out, F1, not_214_out);
  and and_30 (and_30_out, not_215_out, not_216_out, not_217_out, not_218_out, not_219_out, not_220_out, F5, not_221_out, not_222_out, F2, not_223_out, not_224_out);
  and and_31 (and_31_out, not_225_out, not_226_out, not_227_out, not_228_out, not_229_out, not_230_out, F5, not_231_out, not_232_out, F2, not_233_out, F0);
  and and_32 (and_32_out, not_234_out, not_235_out, not_236_out, not_237_out, not_238_out, not_239_out, F5, not_240_out, not_241_out, F2, F1, F0);
  and and_33 (and_33_out, not_242_out, not_243_out, not_244_out, not_245_out, not_246_out, not_247_out, F5, not_248_out, F3, not_249_out, F1, not_250_out);
  and and_34 (and_34_out, not_251_out, not_252_out, not_253_out, not_254_out, not_255_out, not_256_out, F5, not_257_out, F3, not_258_out, F1, F0);
  and and_35 (and_35_out, not_259_out, not_260_out, not_261_out, not_262_out, not_263_out, not_264_out, not_265_out, not_266_out, F3, F2, not_267_out, not_268_out);
  and and_36 (and_36_out, not_269_out, not_270_out, not_271_out, OP2, not_272_out, not_273_out);
  and and_37 (and_37_out, not_274_out, not_275_out, not_276_out, OP2, not_277_out, OP0);
  and and_38 (and_38_out, not_278_out, not_279_out, not_280_out, not_281_out, not_282_out, not_283_out, F5, not_284_out, not_285_out, F2, F1, not_286_out);
  or or_1 (R1_Used, and_1_out, and_2_out, and_3_out, and_4_out, and_5_out, and_6_out, and_7_out, and_8_out, and_9_out, and_10_out, and_11_out, and_12_out, and_13_out, and_14_out, and_15_out, and_16_out, and_17_out, and_18_out, and_19_out, and_20_out, and_21_out, and_22_out, and_23_out);
  or or_2 (R2_Used, and_24_out, and_25_out, and_26_out, and_27_out, and_28_out, and_29_out, and_30_out, and_31_out, and_32_out, and_33_out, and_34_out, and_35_out, and_36_out, and_37_out, and_38_out);
endmodule

module \源寄存器控制器  (
  input  [5:0] OP,
  input  [5:0] Func,
  output R1_Used,
  output R2_Used
);

  \源寄存器使用情况  \u_源寄存器使用情况_1  (
    .OP0(OP[0]), .OP1(OP[1]), .OP2(OP[2]), .OP3(OP[3]), .OP4(OP[4]), .OP5(OP[5]), .F0(Func[0]), .F1(Func[1]),
    .F2(Func[2]), .F3(Func[3]), .F4(Func[4]), .F5(Func[5]), .R1_Used(R1_Used), .R2_Used(R2_Used));
endmodule

module \数据相关检测  (
  input  R1_Used,
  input  [4:0] R1_num,
  input  R2_Used,
  input  [4:0] R2_num,
  input  [4:0] Ex_WrtieReg_num,
  input  EN,
  input  Ex_RegWrite,
  input  Ex_MemToReg,
  input  [4:0] Mem_WrtieReg_num,
  input  Mem_RegWrite,
  input  Mem_MemToReg,
  input  MemWrite,
  input  CLK,
  input  RST,
  output LoadUse,
  output [1:0] R1_Forward,
  output [1:0] R2_Forward,
  output [1:0] StoreForward
);

  wire and_1_out, and_2_out, and_3_out, and_4_out, and_5_out, and_6_out, and_7_out, and_8_out, and_9_out,
       and_10_out, and_11_out, and_12_out, comparator_1_eq, comparator_2_eq, comparator_3_eq,
       comparator_4_eq, comparator_5_eq, comparator_6_eq, not_1_out, not_2_out, not_3_out, or_1_out;
  wire [1:0] priority_encoder_1_out, priority_encoder_2_out, priority_encoder_3_out;

  Comparator #(.width(5)) comparator_1 (.a({5{1'b0}}), .b(R1_num), .eq(comparator_1_eq));  // open: gt, lt
  Comparator #(.width(5)) comparator_2 (.a(R1_num), .b(Ex_WrtieReg_num), .eq(comparator_2_eq));  // open: gt, lt
  Comparator #(.width(5)) comparator_3 (.a({5{1'b0}}), .b(R2_num), .eq(comparator_3_eq));  // open: gt, lt
  Comparator #(.width(5)) comparator_4 (.a(R2_num), .b(Ex_WrtieReg_num), .eq(comparator_4_eq));  // open: gt, lt
  Comparator #(.width(5)) comparator_5 (.a(R1_num), .b(Mem_WrtieReg_num), .eq(comparator_5_eq));  // open: gt, lt
  Comparator #(.width(5)) comparator_6 (.a(R2_num), .b(Mem_WrtieReg_num), .eq(comparator_6_eq));  // open: gt, lt
  not not_1 (not_1_out, comparator_1_eq);
  not not_2 (not_2_out, comparator_3_eq);
  not not_3 (not_3_out, Mem_MemToReg);
  and and_1 (and_1_out, R1_Used, not_1_out, comparator_2_eq, Ex_RegWrite);
  and and_2 (and_2_out, R2_Used, not_2_out, comparator_4_eq, Ex_RegWrite);
  and and_3 (and_3_out, R1_Used, not_1_out, comparator_5_eq, Mem_RegWrite);
  and and_4 (and_4_out, R2_Used, not_2_out, comparator_6_eq, Mem_RegWrite);
  and and_5 (and_5_out, MemWrite, not_2_out, comparator_4_eq, Ex_RegWrite);
  and and_6 (and_6_out, MemWrite, not_2_out, comparator_6_eq, Mem_RegWrite);
  and and_7 (and_7_out, and_3_out, Mem_MemToReg);
  and and_8 (and_8_out, and_3_out, not_3_out);
  and and_9 (and_9_out, and_4_out, Mem_MemToReg);
  and and_10 (and_10_out, and_4_out, not_3_out);
  and and_11 (and_11_out, Mem_MemToReg, and_6_out);
  and and_12 (and_12_out, not_3_out, and_6_out);
  or or_1 (or_1_out, and_1_out, and_5_out, and_2_out);
  and and_13 (LoadUse, or_1_out, Ex_MemToReg);
  Priority_Encoder #(.select(2)) priority_encoder_1 (
    .in0(1'b1), .in1(and_7_out), .in2(and_8_out), .in3(and_1_out), .out(priority_encoder_1_out), .en_in(1'b1));  // open: gs, en_out
  Priority_Encoder #(.select(2)) priority_encoder_2 (
    .in0(1'b1), .in1(and_9_out), .in2(and_10_out), .in3(and_2_out), .out(priority_encoder_2_out), .en_in(1'b1));  // open: gs, en_out
  Priority_Encoder #(.select(2)) priority_encoder_3 (
    .in0(1'b1), .in1(and_11_out), .in2(and_12_out), .in3(and_5_out), .out(priority_encoder_3_out),
    .en_in(1'b1));  // open: gs, en_out
  Register #(.width(2)) register_1 (.D(priority_encoder_1_out), .en(EN), .Q(R1_Forward), .clk(CLK), .clr(RST));
  Register #(.width(2)) register_2 (.D(priority_encoder_2_out), .en(EN), .Q(R2_Forward), .clk(CLK), .clr(RST));
  Register #(.width(2)) register_3 (.D(priority_encoder_3_out), .en(EN), .Q(StoreForward), .clk(CLK), .clr(RST));
endmodule

module \动态分支预测  (
);

  wire and_1_out, and_2_out, and_3_out, and_4_out, and_5_out, and_6_out, and_7_out, and_9_out, Beq, Blez,
       Bne, Branch, BubbleClr, CLK, comparator_1_eq, comparator_2_eq, comparator_3_eq, comparator_4_eq,
       comparator_5_eq, comparator_6_eq, comparator_7_eq, comparator_8_eq, Dest_Branch, Dest_JMP, Dest_JR,
       Disp, EN, Equal, Ex_MemToReg, \ex_mem流水接口_1_halt_2 , \ex_mem流水接口_1_jal_2 , \ex_mem流水接口_1_memwrite_2 ,
       \ex_mem流水接口_1_regdst_2 , \ex_mem流水接口_1_sb_2 , EX_Pred, Ex_RegWrite, Go, Halt, HaltOrRST, ID_EX_Clr,
       ID_EX_EN, \id_ex流水接口_1_alusrcb_2 , \id_ex流水接口_1_halt_2 , \id_ex流水接口_1_jal_2 ,
       \id_ex流水接口_1_memwrite_2 , \id_ex流水接口_1_regdst_2 , \id_ex流水接口_1_sb_2 , \id_ex流水接口_1_signedext_2 ,
       ID_Pred, IF_ID_Clr, IF_ID_EN, JMP, JR, Lez, LoadUse, Mem_MemToReg, Mem_RegWrite,
       \mem_wb流水接口_1_halt_2 , \mem_wb流水接口_1_jal_2 , \mem_wb流水接口_1_regdst_2 , MemWrite, not_1_out, not_2_out,
       not_3_out, not_6_out, not_7_out, not_8_out, Pred, R1_Used, R2_Used, RegWrite, RST, Success,
       \硬布线控制器_1_alu_src , \硬布线控制器_1_beq , \硬布线控制器_1_blez , \硬布线控制器_1_bne , \硬布线控制器_1_jal , \硬布线控制器_1_jmp ,
       \硬布线控制器_1_jr , \硬布线控制器_1_memtoreg , \硬布线控制器_1_regdst , \硬布线控制器_1_regwrite , \硬布线控制器_1_sb ,
       \硬布线控制器_1_signedext , \硬布线控制器_1_syscall ;
  wire [1:0] R1_Forward, R2_Forward, StoreForward;
  wire [3:0] decoder_1_out0, \id_ex流水接口_1_aluop_2 , multiplexer_19_out, \硬布线控制器_1_alu_op ;
  wire [4:0] Ex_WriteReg_num, Mem_WriteReg_num, multiplexer_6_out, multiplexer_7_out, multiplexer_10_out,
       multiplexer_16_out, R1_num, R2_num;
  wire [15:0] \LoadUse气泡数 , \总周期数 , \无条件分支数 , \条件分支成功数 ;
  wire [31:0] AluA, AluB, and_8_out, bit_extender_1_out, BranchAddr, CNT, Dest_PC, Ex_Alu, Ex_IR,
       \ex_mem流水接口_1_b_2 , \ex_mem流水接口_1_ir_2 , EX_PC, EX_PC_, \id_ex流水接口_1_b_2 , \id_ex流水接口_1_imm_2 , ID_PC,
       ID_PC_, \if_id流水接口_1_ir , IF_PC, IF_PC_, JumpPC, LedData, Mem_Alu, MEM_PC, Mem_ReadData,
       \mem_wb流水接口_1_ir_2 , mips_alu_1_result, mips_ram_1_p8, mips_regifile_1_r1, mips_regifile_1_r2,
       multiplexer_2_out, multiplexer_3_out, multiplexer_8_out, multiplexer_12_out, multiplexer_13_out,
       multiplexer_14_out, multiplexer_17_out, multiplexer_20_out, multiplexer_21_out, multiplexer_22_out,
       multiplexer_23_out, PC_In, R1, rom_1_data, shifter_1_out, WB_PC, \分支预测转换_1_pcout ;

  Button \u_总复位  (.out(RST));
  Button u_Go (.out(Go));
  Clock clock_1 (.out(CLK));
  Multiplexer #(.width(32), .enable("false")) multiplexer_1 (
    .in0(multiplexer_2_out), .in1(multiplexer_3_out), .out(JumpPC), .sel(JMP));
  Multiplexer #(.width(32), .enable("false")) multiplexer_2 (
    .in0(EX_PC), .in1(BranchAddr), .out(multiplexer_2_out), .sel(Branch));
  Multiplexer #(.width(32), .enable("false")) multiplexer_3 (
    .in0({EX_PC[31:28], Ex_IR[25:0], 2'b00}), .in1(R1), .out(multiplexer_3_out), .sel(JR));
  not not_1 (not_1_out, Equal);
  Hex_Digit_Display hex_digit_display_1 (.value(LedData[27:24]));  // open: dp
  Hex_Digit_Display hex_digit_display_2 (.value(LedData[31:28]));  // open: dp
  Register #(.width(32)) PC (.D(PC_In), .en(IF_ID_EN), .Q(IF_PC_), .clk(CLK), .clr(RST));
  and and_1 (and_1_out, Beq, Equal);
  and and_2 (and_2_out, Bne, not_1_out);
  and and_3 (and_3_out, Blez, Lez);
  Counter #(.width(16), .max('hffff)) counter_1 (.count(EN), .Q(\总周期数 ), .clk(CLK), .clr(RST));  // open: load, D, carry
  Hex_Digit_Display hex_digit_display_3 (.value(LedData[19:16]));  // open: dp
  Hex_Digit_Display hex_digit_display_4 (.value(LedData[23:20]));  // open: dp
  not not_2 (not_2_out, Halt);
  or or_1 (Branch, and_1_out, and_2_out, and_3_out);
  Hex_Digit_Display hex_digit_display_5 (.value(LedData[11:8]));  // open: dp
  Hex_Digit_Display hex_digit_display_6 (.value(LedData[15:12]));  // open: dp
  ROM #(.addrWidth(10), .dataWidth(32)) rom_1 (.addr(IF_PC_[11:2]), .data(rom_1_data));  // open: sel
  Adder #(.width(32)) adder_1 (.a(IF_PC_), .b(32'h4), .out(IF_PC));  // open: cin, cout
  \数据相关检测  \u_数据相关检测_1  (
    .R1_Used(R1_Used), .R1_num(R1_num), .R2_Used(R2_Used), .R2_num(R2_num),
    .Ex_WrtieReg_num(Ex_WriteReg_num), .Ex_RegWrite(Ex_RegWrite), .Ex_MemToReg(Ex_MemToReg),
    .Mem_WrtieReg_num(Mem_WriteReg_num), .Mem_RegWrite(Mem_RegWrite), .Mem_MemToReg(Mem_MemToReg),
    .MemWrite(MemWrite), .EN(not_2_out), .CLK(CLK), .RST(HaltOrRST), .LoadUse(LoadUse),
    .R1_Forward(R1_Forward), .R2_Forward(R2_Forward), .StoreForward(StoreForward));
  and and_4 (and_4_out, EN, ID_EX_EN, not_3_out);
  not not_3 (not_3_out, LoadUse);
  not not_4 (ID_EX_EN, Halt);
  and and_5 (and_5_out, Halt, Go);
  Counter #(.width(16), .max('hffff)) counter_2 (
    .count(and_6_out), .Q(\无条件分支数 ), .clk(CLK), .clr(RST));  // open: load, D, carry
  and and_6 (and_6_out, JMP, IF_ID_EN);
  Hex_Digit_Display hex_digit_display_7 (.value(LedData[3:0]));  // open: dp
  Hex_Digit_Display hex_digit_display_8 (.value(LedData[7:4]));  // open: dp
  or or_2 (BubbleClr, JMP, Branch);
  not not_5 (IF_ID_Clr, Success);
  or or_3 (ID_EX_Clr, IF_ID_Clr, LoadUse);
  or or_4 (IF_ID_EN, and_4_out, and_5_out);
  \IF_ID流水接口  \if_id流水接口_1  (
    .Inst(rom_1_data), .PC(IF_PC), .CLK(CLK), .IR(\if_id流水接口_1_ir ), .PC_2(ID_PC), .clr(IF_ID_Clr),
    .EN(IF_ID_EN), .RST(RST), .PC_(IF_PC_), .PC__2(ID_PC_), .Pred(Pred), .Pred_2(ID_Pred));
  and and_7 (and_7_out, Branch, EN);
  // Probe on \总周期数 
  // Probe on \无条件分支数 
  // Probe on \条件分支成功数 
  \源寄存器控制器  \u_源寄存器控制器_1  (
    .OP(\if_id流水接口_1_ir [31:26]), .Func(\if_id流水接口_1_ir [5:0]), .R1_Used(R1_Used), .R2_Used(R2_Used));
  Multiplexer #(.width(5), .enable("false")) multiplexer_4 (
    .in0(\if_id流水接口_1_ir [25:21]), .in1(5'b00010), .out(R1_num), .sel(\硬布线控制器_1_syscall ));
  Multiplexer #(.width(5), .enable("false")) multiplexer_5 (
    .in0(\if_id流水接口_1_ir [20:16]), .in1(5'b00100), .out(R2_num), .sel(\硬布线控制器_1_syscall ));
  Multiplexer #(.width(5), .enable("false")) multiplexer_6 (
    .in0(\mem_wb流水接口_1_ir_2 [20:16]), .in1(\mem_wb流水接口_1_ir_2 [15:11]), .out(multiplexer_6_out),
    .sel(\mem_wb流水接口_1_regdst_2 ));
  Multiplexer #(.width(5), .enable("false")) multiplexer_7 (
    .in0(multiplexer_6_out), .in1({5{1'b1}}), .out(multiplexer_7_out), .sel(\mem_wb流水接口_1_jal_2 ));
  Counter #(.width(16), .max('hffff)) counter_3 (
    .count(and_7_out), .Q(\条件分支成功数 ), .clk(CLK), .clr(RST));  // open: load, D, carry
  \硬布线控制器  \u_硬布线控制器_1  (
    .Func(\if_id流水接口_1_ir [5:0]), .OP(\if_id流水接口_1_ir [31:26]), .ALU_OP(\硬布线控制器_1_alu_op ),
    .MemToReg(\硬布线控制器_1_memtoreg ), .MemWrite(MemWrite), .ALU_SRC(\硬布线控制器_1_alu_src ),
    .RegWrite(\硬布线控制器_1_regwrite ), .SysCALL(\硬布线控制器_1_syscall ), .SignedExt(\硬布线控制器_1_signedext ),
    .RegDst(\硬布线控制器_1_regdst ), .JR(\硬布线控制器_1_jr ), .JMP(\硬布线控制器_1_jmp ), .Beq(\硬布线控制器_1_beq ),
    .JAL(\硬布线控制器_1_jal ), .Bne(\硬布线控制器_1_bne ), .SB(\硬布线控制器_1_sb ), .BLEZ(\硬布线控制器_1_blez ));
  assign bit_extender_1_out = {{16{\if_id流水接口_1_ir [15]}}, \if_id流水接口_1_ir [15:0]};  // Bit_Extender bit_extender_1
  Multiplexer #(.width(32), .enable("false")) multiplexer_8 (
    .in0(Mem_ReadData), .in1(WB_PC), .out(multiplexer_8_out), .sel(\mem_wb流水接口_1_jal_2 ));
  // Probe on \LoadUse气泡数 
  MIPS_Regifile mips_regifile_1 (
    .Din(multiplexer_8_out), .Clk(CLK), .R1(mips_regifile_1_r1), .R2(mips_regifile_1_r2), .WE(RegWrite),
    .W_num(multiplexer_7_out), .R1_num(R1_num), .R2_num(R2_num));
  Register #(.width(32)) register_1 (.D(AluB), .en(Disp), .Q(LedData), .clk(CLK), .clr(RST));
  \ID_EX流水接口  \id_ex流水接口_1  (
    .RegWrite(\硬布线控制器_1_regwrite ), .RegDst(\硬布线控制器_1_regdst ), .JAL(\硬布线控制器_1_jal ), .SB(\硬布线控制器_1_sb ),
    .MemToReg(\硬布线控制器_1_memtoreg ), .MemWrite(MemWrite), .AluOp(\硬布线控制器_1_alu_op ),
    .AluSrcB(\硬布线控制器_1_alu_src ), .SignedExt(\硬布线控制器_1_signedext ), .Halt(\硬布线控制器_1_syscall ),
    .JMP(\硬布线控制器_1_jmp ), .JR(\硬布线控制器_1_jr ), .Beq(\硬布线控制器_1_beq ), .Bne(\硬布线控制器_1_bne ),
    .Blez(\硬布线控制器_1_blez ), .IR(\if_id流水接口_1_ir ), .PC(ID_PC), .A(mips_regifile_1_r1),
    .B(mips_regifile_1_r2), .Imm(bit_extender_1_out), .CLK(CLK), .RegWrite_2(Ex_RegWrite),
    .RegDst_2(\id_ex流水接口_1_regdst_2 ), .JAL_2(\id_ex流水接口_1_jal_2 ), .SB_2(\id_ex流水接口_1_sb_2 ),
    .MemToReg_2(Ex_MemToReg), .MemWrite_2(\id_ex流水接口_1_memwrite_2 ), .AluOp_2(\id_ex流水接口_1_aluop_2 ),
    .AluSrcB_2(\id_ex流水接口_1_alusrcb_2 ), .SignedExt_2(\id_ex流水接口_1_signedext_2 ),
    .Halt_2(\id_ex流水接口_1_halt_2 ), .JMP_2(JMP), .JR_2(JR), .Beq_2(Beq), .Bne_2(Bne), .Blez_2(Blez),
    .IR_2(Ex_IR), .PC_2(EX_PC), .A_2(R1), .B_2(\id_ex流水接口_1_b_2 ), .Imm_2(\id_ex流水接口_1_imm_2 ),
    .clr(ID_EX_Clr), .EN(ID_EX_EN), .RST(HaltOrRST), .PC_(ID_PC_), .PC__2(EX_PC_), .Pred(ID_Pred),
    .Pred_2(EX_Pred));
  assign and_8_out = \id_ex流水接口_1_imm_2  & 32'hffff;  // AND_Gate and_8, 32 bits wide
  Multiplexer #(.select(2), .width(32), .enable("false")) multiplexer_9 (
    .in0(R1), .in1(Mem_ReadData), .in2(Mem_Alu), .in3(Ex_Alu), .out(AluA), .sel(R1_Forward));
  Counter #(.width(16), .max('hffff)) counter_4 (
    .count(and_9_out), .Q(\LoadUse气泡数 ), .clk(CLK), .clr(RST));  // open: load, D, carry
  and and_9 (and_9_out, LoadUse, EN);
  Multiplexer #(.width(5), .enable("false")) multiplexer_10 (
    .in0(Ex_IR[20:16]), .in1(Ex_IR[15:11]), .out(multiplexer_10_out), .sel(\id_ex流水接口_1_regdst_2 ));
  Multiplexer #(.width(5), .enable("false")) multiplexer_11 (
    .in0(multiplexer_10_out), .in1({5{1'b1}}), .out(Ex_WriteReg_num), .sel(\id_ex流水接口_1_jal_2 ));
  Multiplexer #(.width(32), .enable("false")) multiplexer_12 (
    .in0(\id_ex流水接口_1_b_2 ), .in1(multiplexer_13_out), .out(multiplexer_12_out), .sel(\id_ex流水接口_1_alusrcb_2 ));
  Multiplexer #(.width(32), .enable("false")) multiplexer_13 (
    .in0(and_8_out), .in1(\id_ex流水接口_1_imm_2 ), .out(multiplexer_13_out), .sel(\id_ex流水接口_1_signedext_2 ));
  // Mips_Probe mips_probe_1: pin names not known; wires that end beside it: Ex_IR
  Shifter #(.width(32)) shifter_1 (.in(\id_ex流水接口_1_imm_2 ), .\dist (5'b00010), .out(shifter_1_out));
  Multiplexer #(.select(2), .width(32), .enable("false")) multiplexer_14 (
    .in0(\id_ex流水接口_1_b_2 ), .in1(Mem_ReadData), .in2(Mem_Alu), .in3(Ex_Alu), .out(multiplexer_14_out),
    .sel(StoreForward));
  Multiplexer #(.select(2), .width(32), .enable("false")) multiplexer_15 (
    .in0(multiplexer_12_out), .in1(Mem_ReadData), .in2(Mem_Alu), .in3(Ex_Alu), .out(AluB), .sel(R2_Forward));
  Adder #(.width(32)) adder_2 (.a(EX_PC), .b(shifter_1_out), .out(BranchAddr));  // open: cin, cout
  MIPS_ALU mips_alu_1 (
    .X(AluA), .Y(AluB), .AluOP(\id_ex流水接口_1_aluop_2 ), .Equal(Equal), .Result(mips_alu_1_result),
    .shamt(Ex_IR[10:6]), .LEZ(Lez));  // open: Result_2
  Counter #(.width(32), .max('hffffffff)) counter_5 (
    .count(EN), .Q(CNT), .clk(CLK), .clr(RST));  // open: load, D, carry
  // Probe on CNT
  Comparator #(.width(32)) comparator_1 (.a(AluA), .b(32'h22), .eq(comparator_1_eq));  // open: gt, lt
  Comparator #(.width(6)) comparator_2 (.a(Ex_IR[31:26]), .b(6'b000100), .eq(comparator_2_eq));  // open: gt, lt
  Comparator #(.width(6)) comparator_3 (.a(Ex_IR[31:26]), .b(6'b000101), .eq(comparator_3_eq));  // open: gt, lt
  Comparator #(.width(6)) comparator_4 (.a(Ex_IR[31:26]), .b(6'b000110), .eq(comparator_4_eq));  // open: gt, lt
  Comparator #(.width(6)) comparator_5 (.a(Ex_IR[31:26]), .b(6'b000010), .eq(comparator_5_eq));  // open: gt, lt
  Comparator #(.width(6)) comparator_6 (.a(Ex_IR[31:26]), .b(6'b000011), .eq(comparator_6_eq));  // open: gt, lt
  Comparator #(.width(6)) comparator_7 (.a(Ex_IR[31:26]), .b({6{1'b0}}), .eq(comparator_7_eq));  // open: gt, lt
  Comparator #(.width(6)) comparator_8 (.a(Ex_IR[5:0]), .b(6'b001000), .eq(comparator_8_eq));  // open: gt, lt
  \EX_MEM流水接口  \ex_mem流水接口_1  (
    .RegWrite(Ex_RegWrite), .RegDst(\id_ex流水接口_1_regdst_2 ), .JAL(\id_ex流水接口_1_jal_2 ),
    .SB(\id_ex流水接口_1_sb_2 ), .MemToReg(Ex_MemToReg), .MemWrite(\id_ex流水接口_1_memwrite_2 ), .IR(Ex_IR),
    .PC(EX_PC), .ALU(mips_alu_1_result), .B(multiplexer_14_out), .CLK(CLK), .RegWrite_2(Mem_RegWrite),
    .RegDst_2(\ex_mem流水接口_1_regdst_2 ), .JAL_2(\ex_mem流水接口_1_jal_2 ), .SB_2(\ex_mem流水接口_1_sb_2 ),
    .MemToReg_2(Mem_MemToReg), .MemWrite_2(\ex_mem流水接口_1_memwrite_2 ), .IR_2(\ex_mem流水接口_1_ir_2 ),
    .PC_2(MEM_PC), .ALU_2(Ex_Alu), .B_2(\ex_mem流水接口_1_b_2 ), .clr(1'b0), .EN(EN), .Halt(Halt),
    .Halt_2(\ex_mem流水接口_1_halt_2 ), .RST(HaltOrRST));
  Decoder #(.select(2), .enable("false")) decoder_1 (
    .out0(decoder_1_out0[0]), .out1(decoder_1_out0[1]), .out2(decoder_1_out0[2]), .out3(decoder_1_out0[3]),
    .sel(Ex_Alu[1:0]));
  and and_10 (Disp, comparator_1_eq, \id_ex流水接口_1_halt_2 );
  not not_6 (not_6_out, comparator_1_eq);
  or or_5 (Dest_Branch, comparator_2_eq, comparator_3_eq, comparator_4_eq);
  and and_11 (Dest_JR, comparator_7_eq, comparator_8_eq);
  Multiplexer #(.width(5), .enable("false")) multiplexer_16 (
    .in0(\ex_mem流水接口_1_ir_2 [20:16]), .in1(\ex_mem流水接口_1_ir_2 [15:11]), .out(multiplexer_16_out),
    .sel(\ex_mem流水接口_1_regdst_2 ));
  Multiplexer #(.width(32), .enable("false")) multiplexer_17 (
    .in0(\ex_mem流水接口_1_b_2 ),
    .in1({\ex_mem流水接口_1_b_2 [7:0], \ex_mem流水接口_1_b_2 [7:0], \ex_mem流水接口_1_b_2 [7:0], \ex_mem流水接口_1_b_2 [7:0]}),
    .out(multiplexer_17_out), .sel(\ex_mem流水接口_1_sb_2 ));
  and and_12 (Halt, not_6_out, \id_ex流水接口_1_halt_2 );
  or or_6 (Dest_JMP, comparator_5_eq, comparator_6_eq, Dest_JR);
  Multiplexer #(.width(5), .enable("false")) multiplexer_18 (
    .in0(multiplexer_16_out), .in1({5{1'b1}}), .out(Mem_WriteReg_num), .sel(\ex_mem流水接口_1_jal_2 ));
  Multiplexer #(.width(4), .enable("false")) multiplexer_19 (
    .in0(4'b1111), .in1(decoder_1_out0), .out(multiplexer_19_out), .sel(\ex_mem流水接口_1_sb_2 ));
  // Probe on IF_PC[11:0]
  // Probe on ID_PC[11:0]
  // Probe on EX_PC[11:0]
  // Probe on MEM_PC[11:0]
  // Probe on WB_PC[11:0]
  // MIPS_RAM mips_ram_1: pin names not known; wires that end beside it: Ex_Alu[11:2], multiplexer_17_out, \ex_mem流水接口_1_memwrite_2 , multiplexer_19_out, CLK, 1'b1, RST, mips_ram_1_p8
  Multiplexer #(.width(32), .enable("false")) multiplexer_20 (
    .in0({EX_PC[31:28], Ex_IR[25:0], 2'b00}), .in1(AluA), .out(multiplexer_20_out), .sel(Dest_JR));
  Multiplexer #(.width(32), .enable("false")) multiplexer_21 (
    .in0(Ex_Alu), .in1(mips_ram_1_p8), .out(multiplexer_21_out), .sel(Mem_MemToReg));
  \分支预测转换  \u_分支预测转换_1  (
    .jump(BubbleClr), .pc(IF_PC_), .predict(Pred), .CLK(CLK), .EX_IR(Ex_IR), .pastpc(EX_PC_),
    .pcout(\分支预测转换_1_pcout ), .pastnpc(Dest_PC));
  xnor xnor_1 (Success, BubbleClr, EX_Pred);
  Multiplexer #(.width(32), .enable("false")) multiplexer_22 (
    .in0(EX_PC), .in1(BranchAddr), .out(multiplexer_22_out), .sel(Dest_Branch));
  \MEM_WB流水接口  \mem_wb流水接口_1  (
    .RegWrite(Mem_RegWrite), .RegDst(\ex_mem流水接口_1_regdst_2 ), .JAL(\ex_mem流水接口_1_jal_2 ),
    .IR(\ex_mem流水接口_1_ir_2 ), .PC(MEM_PC), .ALU(Ex_Alu), .MD(multiplexer_21_out), .CLK(CLK),
    .RegWrite_2(RegWrite), .RegDst_2(\mem_wb流水接口_1_regdst_2 ), .JAL_2(\mem_wb流水接口_1_jal_2 ),
    .IR_2(\mem_wb流水接口_1_ir_2 ), .PC_2(WB_PC), .ALU_2(Mem_Alu), .MD_2(Mem_ReadData), .clr(1'b0), .EN(EN),
    .Halt(\ex_mem流水接口_1_halt_2 ), .Halt_2(\mem_wb流水接口_1_halt_2 ), .RST(RST));
  Multiplexer #(.width(32), .enable("false")) multiplexer_23 (
    .in0(IF_PC), .in1(\分支预测转换_1_pcout ), .out(multiplexer_23_out), .sel(Pred));
  Multiplexer #(.width(32), .enable("false")) multiplexer_24 (
    .in0(multiplexer_22_out), .in1(multiplexer_20_out), .out(Dest_PC), .sel(Dest_JMP));
  not not_7 (not_7_out, Go);
  not not_8 (not_8_out, EN);
  Multiplexer #(.width(32), .enable("false")) multiplexer_25 (
    .in0(JumpPC), .in1(multiplexer_23_out), .out(PC_In), .sel(Success));
  nand nand_1 (EN, \mem_wb流水接口_1_halt_2 , not_7_out);
  or or_7 (HaltOrRST, not_8_out, RST);

  // Other names for the same wires on the sheet: JmpAddr[31:2] = {EX_PC[31:28], Ex_IR[25:0]}; PC_EN = IF_ID_EN

  // Notes on the sheet:
  //   数码管输出应该用寄存器锁存，否则显示数据只能一闪而过
  //   可以通过项目增加Logisim库的方式将前几次实验完成的电路作为子电路引入到本电路中使用
  //   指令存储器
  //   contents of rom_1 (hex, n*v repeats v):
  //   20110001 8000c05 20110001 20120002 20130003 8000c09 20110001 20120002 20130003 8000c0d 20110001
  //   20120002 20130003 8000c11 20110001 20120002 20130003 c000cf5 20100001 20110001 118fc0 112020
  //   20020022 c 118882 12200001 8000c15 112020 20020022 c 20110001 118880 112020 20020022 c 12200001
  //   8000c1f 20110001 118fc0 112020 20020022 c 1188c3 112020 20020022 c 118903 112020 20020022 c 118903
  //   112020 20020022 c 118903 112020 20020022 c 118903 112020 20020022 c 118903 112020 20020022 c 118903
  //   112020 20020022 c 118903 112020 20020022 c 20100001 109fc0 139fc3 8021 2012000c 24160003 26100001
  //   3210000f 20080008 20090001 139900 2709825 132020 20020022 c 1094022 1500fff9 22100001 2018000f
  //   2188024 108700 20080008 20090001 139902 2709825 132021 20020022 c 1094022 1500fff9 108702 2c9b022
  //   12c00001 8000c50 4020 1084027 84400 3508ffff 82021 20020022 c 2010ffff 20110000 ae300000 22100001
  //   22310004 ae300000 22100001 22310004 ae300000 22100001 22310004 ae300000 22100001 22310004 ae300000
  //   22100001 22310004 ae300000 22100001 22310004 ae300000 22100001 22310004 ae300000 22100001 22310004
  //   ae300000 22100001 22310004 ae300000 22100001 22310004 ae300000 22100001 22310004 ae300000 22100001
  //   22310004 ae300000 22100001 22310004 ae300000 22100001 22310004 ae300000 22100001 22310004 ae300000
  //   22100001 22310004 22100001 8020 2011003c 8e130000 8e340000 274402a 11000002 ae330000 ae140000
  //   2231fffc 1611fff8 102020 20020022 c 22100004 2011003c 1611fff2 20020032 c 2008ffff 20117777 112020
  //   20020022 c 200b0010 2288826 112020 20020022 c 216bffff 1560fffa 2002000a c 2008ffff 20117777 112020
  //   20020022 c 200b0010 3a31ffff 112020 20020022 c 216bffff 1560fffa 2002000a c 20090000 200b0020
  //   20110000 20120001 a1310000 112020 20020022 c 2328820 21290001 216bffff 1560fff8 200b0008 20090000
  //   8d310000 112020 20020022 c 21290004 216bffff 1560fff9 2002000a c 2011fff1 112020 20020022 c 22310001
  //   1a20fffb 2002000a c 2002000a c 20100000 22100001 102020 20020022 c 22100002 102020 20020022 c
  //   22100003 102020 20020022 c 22100004 102020 20020022 c 22100005 102020 20020022 c 22100006 102020
  //   20020022 c 22100007 102020 20020022 c 22100008 102020 20020022 20020022 c 3e00008
  //   数码管输出
  //   指令字
  //   总复位信号应将除ROM以外所有存储组件全部清零
endmodule

module \状态机  (
  input  \原预测状态高位 ,
  input  \原预测状态低位 ,
  input  \实际跳转情况 ,
  output \新状态高位 ,
  output \新状态低位 
);

  wire and_1_out, and_2_out, and_3_out, and_4_out, not_1_out, not_2_out, not_3_out, not_4_out, not_5_out;

  not not_1 (not_1_out, \原预测状态低位 );
  not not_2 (not_2_out, \原预测状态高位 );
  not not_3 (not_3_out, \原预测状态低位 );
  not not_4 (not_4_out, \原预测状态低位 );
  not not_5 (not_5_out, \实际跳转情况 );
  and and_1 (and_1_out, \原预测状态低位 , \实际跳转情况 );
  and and_2 (and_2_out, \原预测状态高位 , not_1_out);
  and and_3 (and_3_out, not_2_out, not_3_out, \实际跳转情况 );
  and and_4 (and_4_out, \原预测状态高位 , not_4_out, not_5_out);
  or or_1 (\新状态高位 , and_1_out, and_2_out);
  or or_2 (\新状态低位 , and_3_out, and_4_out);
endmodule

module Max3 (
  input  [15:0] Y,
  input  [15:0] X,
  input  [2:0] Y_num,
  input  [2:0] X_num,
  output [15:0] MAX,
  output [2:0] Max_num
);

  wire comparator_1_eq, comparator_1_gt, or_1_out;

  Multiplexer #(.width(16), .enable("false")) multiplexer_1 (.in0(Y), .in1(X), .out(MAX), .sel(or_1_out));
  Comparator #(.width(16), .mode("unsigned")) comparator_1 (
    .a(X), .b(Y), .gt(comparator_1_gt), .eq(comparator_1_eq));  // open: lt
  or or_1 (or_1_out, comparator_1_gt, comparator_1_eq);
  Multiplexer #(.width(3), .enable("false")) multiplexer_2 (.in0(Y_num), .in1(X_num), .out(Max_num), .sel(or_1_out));

  // Notes on the sheet:
  //   输出两个输入中的较大值，并输出较大值的3位编号
endmodule

module \分支预测转换  (
  input  jump,
  input  [31:0] pc,
  input  CLK,
  input  [31:0] EX_IR,
  input  [31:0] pastpc,
  input  [31:0] pastnpc,
  output predict,
  output [31:0] pcout
);

  wire and_2_out, and_3_out, and_4_out, and_5_out, and_6_out, and_7_out, and_8_out, and_18_out, and_19_out,
       and_20_out, and_21_out, and_22_out, and_23_out, and_24_out, and_25_out, and_26_out, and_35_out,
       and_36_out, and_37_out, comparator_1_eq, comparator_2_eq, comparator_3_eq, comparator_4_eq,
       comparator_5_eq, comparator_6_eq, comparator_7_eq, comparator_8_eq, comparator_9_eq, comparator_10_eq,
       comparator_11_eq, comparator_12_eq, comparator_13_eq, comparator_14_eq, comparator_15_eq,
       comparator_16_eq, comparator_17_eq, comparator_18_eq, comparator_19_eq, comparator_20_eq,
       comparator_21_eq, comparator_22_eq, comparator_23_eq, comparator_24_eq, comparator_25_eq,
       decoder_1_out0, decoder_1_out1, decoder_1_out2, decoder_1_out3, decoder_1_out4, decoder_1_out5,
       decoder_1_out6, decoder_1_out7, FULL, HIT1, HIT2, jump2, L0, L1, L2, L3, L4, L5, L6, L7, LH0, LH1,
       LH2, LH3, LH4, LH5, LH6, LH7, not_1_out, not_2_out, not_3_out, not_4_out, not_5_out, not_6_out,
       not_7_out, not_8_out, not_9_out, or_1_out, or_2_out, SEL0, SEL1, SEL2, SEL3, SEL4, SEL5, SEL6, SEL7,
       V0, V1, V2, V3, V4, V5, V6, V7;
  wire [1:0] multiplexer_18_out, register_17_q, register_18_q, register_19_q, register_20_q, register_21_q,
       register_22_q, register_23_q, register_24_q, statein, stateout1, stateout2, \状态机_1_新状态低位 ;
  wire [2:0] controlled_buffer_1_out, max3_1_max_num, max3_2_max_num, max3_3_max_num, max3_4_max_num,
       max3_5_max_num, max3_6_max_num, max3_7_max_num, priority_encoder_1_out;
  wire [15:0] C0, C1, C2, C3, C4, C5, C6, C7, max3_1_max, max3_2_max, max3_3_max, max3_4_max, max3_5_max,
       max3_7_max;
  wire [31:0] addr0, addr1, addr2, addr3, addr4, addr5, addr6, addr7, multiplexer_9_out, multiplexer_10_out,
       multiplexer_11_out, multiplexer_12_out, multiplexer_13_out, multiplexer_14_out, multiplexer_15_out,
       pc0, pc1, pc2, pc3, pc4, pc5, pc6, pc7;

  Max3 max3_1 (.Y(C0), .X(C1), .Y_num(3'b000), .X_num(3'b001), .MAX(max3_1_max), .Max_num(max3_1_max_num));
  Max3 max3_2 (.Y(C2), .X(C3), .Y_num(3'b010), .X_num(3'b011), .MAX(max3_2_max), .Max_num(max3_2_max_num));
  Max3 max3_3 (.Y(C4), .X(C5), .Y_num(3'b100), .X_num(3'b101), .MAX(max3_3_max), .Max_num(max3_3_max_num));
  Max3 max3_4 (.Y(C6), .X(C7), .Y_num(3'b110), .X_num(3'b111), .MAX(max3_4_max), .Max_num(max3_4_max_num));
  and and_1 (FULL, V7, V6, V5, V4, V3, V2, V1, V0);
  Max3 max3_5 (
    .Y(max3_1_max), .X(max3_2_max), .Y_num(max3_1_max_num), .X_num(max3_2_max_num), .MAX(max3_5_max),
    .Max_num(max3_5_max_num));
  Max3 max3_6 (
    .Y(max3_5_max), .X(max3_7_max), .Y_num(max3_5_max_num), .X_num(max3_7_max_num), .Max_num(max3_6_max_num));  // open: MAX
  Max3 max3_7 (
    .Y(max3_3_max), .X(max3_4_max), .Y_num(max3_3_max_num), .X_num(max3_4_max_num), .MAX(max3_7_max),
    .Max_num(max3_7_max_num));
  not not_1 (not_1_out, V0);
  and and_2 (and_2_out, V0, not_2_out);
  not not_2 (not_2_out, V1);
  and and_3 (and_3_out, V0, V1, not_3_out);
  not not_3 (not_3_out, V2);
  and and_4 (and_4_out, V0, V1, V2, not_4_out);
  not not_4 (not_4_out, V3);
  and and_5 (and_5_out, V0, V1, V2, V3, not_5_out);
  not not_5 (not_5_out, V4);
  and and_6 (and_6_out, V0, V1, V2, V3, V4, not_6_out);
  not not_6 (not_6_out, V5);
  and and_7 (and_7_out, V0, V1, V2, V3, V4, V5, not_7_out);
  not not_7 (not_7_out, V6);
  and and_8 (and_8_out, V0, V1, V2, V3, V4, V5, V6, not_8_out);
  not not_8 (not_8_out, V7);
  Comparator #(.width(32)) comparator_1 (.a(pc), .b(pc0), .eq(comparator_1_eq));  // open: gt, lt
  Comparator #(.width(32)) comparator_2 (.a(pc), .b(pc1), .eq(comparator_2_eq));  // open: gt, lt
  Comparator #(.width(32)) comparator_3 (.a(pc), .b(pc2), .eq(comparator_3_eq));  // open: gt, lt
  Comparator #(.width(32)) comparator_4 (.a(pc), .b(pc3), .eq(comparator_4_eq));  // open: gt, lt
  Comparator #(.width(32)) comparator_5 (.a(pc), .b(pc4), .eq(comparator_5_eq));  // open: gt, lt
  Comparator #(.width(32)) comparator_6 (.a(pc), .b(pc5), .eq(comparator_6_eq));  // open: gt, lt
  Comparator #(.width(32)) comparator_7 (.a(pc), .b(pc6), .eq(comparator_7_eq));  // open: gt, lt
  Comparator #(.width(32)) comparator_8 (.a(pc), .b(pc7), .eq(comparator_8_eq));  // open: gt, lt
  assign controlled_buffer_1_out = FULL ? max3_6_max_num : 3'bz;  // Controlled_Buffer controlled_buffer_1
  or or_1 (or_1_out, FULL, HIT1);
  Comparator #(.width(2)) comparator_9 (.a(stateout1), .b(2'b10), .eq(comparator_9_eq));  // open: gt, lt
  Comparator #(.width(2)) comparator_10 (.a(stateout1), .b(2'b11), .eq(comparator_10_eq));  // open: gt, lt
  assign controlled_buffer_1_out = not_9_out ? priority_encoder_1_out : 3'bz;  // Controlled_Buffer controlled_buffer_2
  not not_9 (not_9_out, or_1_out);
  Priority_Encoder priority_encoder_1 (
    .in0(not_1_out), .in1(and_2_out), .in2(and_3_out), .in3(and_4_out), .in4(and_5_out), .in5(and_6_out),
    .in6(and_7_out), .in7(and_8_out), .out(priority_encoder_1_out));  // open: en_in, gs, en_out
  and and_9 (LH0, V0, comparator_1_eq);
  and and_10 (LH1, V1, comparator_2_eq);
  and and_11 (LH2, V2, comparator_3_eq);
  and and_12 (LH3, V3, comparator_4_eq);
  and and_13 (LH4, V4, comparator_5_eq);
  and and_14 (LH5, V5, comparator_6_eq);
  and and_15 (LH6, V6, comparator_7_eq);
  and and_16 (LH7, V7, comparator_8_eq);
  or or_2 (or_2_out, comparator_9_eq, comparator_10_eq);
  Decoder #(.select(3), .enable("false")) decoder_1 (
    .out0(decoder_1_out0), .out1(decoder_1_out1), .out2(decoder_1_out2), .out3(decoder_1_out3),
    .out4(decoder_1_out4), .out5(decoder_1_out5), .out6(decoder_1_out6), .out7(decoder_1_out7),
    .sel(controlled_buffer_1_out));
  or or_3 (HIT1, LH0, LH1, LH2, LH3, LH4, LH5, LH6, LH7);
  and and_17 (predict, HIT1, or_2_out);
  and and_18 (and_18_out, decoder_1_out0, jump2);
  and and_19 (and_19_out, decoder_1_out1, jump2);
  and and_20 (and_20_out, decoder_1_out2, jump2);
  and and_21 (and_21_out, decoder_1_out3, jump2);
  and and_22 (and_22_out, decoder_1_out4, jump2);
  and and_23 (and_23_out, decoder_1_out5, jump2);
  and and_24 (and_24_out, decoder_1_out6, jump2);
  and and_25 (and_25_out, decoder_1_out7, jump2);
  Comparator #(.width(6)) comparator_11 (.a(EX_IR[31:26]), .b({6{1'b0}}), .eq(comparator_11_eq));  // open: gt, lt
  Comparator #(.width(6)) comparator_12 (.a(EX_IR[5:0]), .b(6'b001000), .eq(comparator_12_eq));  // open: gt, lt
  Multiplexer multiplexer_1 (.in0(and_18_out), .in1(L0), .out(SEL0), .sel(HIT2));  // open: en
  Multiplexer multiplexer_2 (.in0(and_19_out), .in1(L1), .out(SEL1), .sel(HIT2));  // open: en
  Multiplexer multiplexer_3 (.in0(and_20_out), .in1(L2), .out(SEL2), .sel(HIT2));  // open: en
  Multiplexer multiplexer_4 (.in0(and_21_out), .in1(L3), .out(SEL3), .sel(HIT2));  // open: en
  Multiplexer multiplexer_5 (.in0(and_22_out), .in1(L4), .out(SEL4), .sel(HIT2));  // open: en
  Multiplexer multiplexer_6 (.in0(and_23_out), .in1(L5), .out(SEL5), .sel(HIT2));  // open: en
  Multiplexer multiplexer_7 (.in0(and_24_out), .in1(L6), .out(SEL6), .sel(HIT2));  // open: en
  Multiplexer multiplexer_8 (.in0(and_25_out), .in1(L7), .out(SEL7), .sel(HIT2));  // open: en
  Comparator #(.width(6)) comparator_13 (.a(EX_IR[31:26]), .b(6'b000111), .eq(comparator_13_eq));  // open: gt, lt
  Comparator #(.width(6)) comparator_14 (.a(EX_IR[31:26]), .b(6'b000100), .eq(comparator_14_eq));  // open: gt, lt
  Comparator #(.width(6)) comparator_15 (.a(EX_IR[31:26]), .b(6'b000101), .eq(comparator_15_eq));  // open: gt, lt
  Comparator #(.width(6)) comparator_16 (.a(EX_IR[31:26]), .b(6'b000010), .eq(comparator_16_eq));  // open: gt, lt
  Comparator #(.width(6)) comparator_17 (.a(EX_IR[31:26]), .b(6'b000011), .eq(comparator_17_eq));  // open: gt, lt
  and and_26 (and_26_out, comparator_11_eq, comparator_12_eq);
  Multiplexer #(.width(32), .enable("false")) multiplexer_9 (
    .in0({32{1'b0}}), .in1(addr0), .out(multiplexer_9_out), .sel(LH0));
  Multiplexer #(.width(32), .enable("false")) multiplexer_10 (
    .in0(multiplexer_9_out), .in1(addr1), .out(multiplexer_10_out), .sel(LH1));
  or or_4 (jump2, comparator_13_eq, comparator_14_eq, comparator_15_eq, comparator_16_eq, comparator_17_eq, and_26_out);
  Comparator #(.width(32)) comparator_18 (.a(pastpc), .b(pc0), .eq(comparator_18_eq));  // open: gt, lt
  Comparator #(.width(32)) comparator_19 (.a(pastpc), .b(pc1), .eq(comparator_19_eq));  // open: gt, lt
  Comparator #(.width(32)) comparator_20 (.a(pastpc), .b(pc2), .eq(comparator_20_eq));  // open: gt, lt
  Comparator #(.width(32)) comparator_21 (.a(pastpc), .b(pc3), .eq(comparator_21_eq));  // open: gt, lt
  Comparator #(.width(32)) comparator_22 (.a(pastpc), .b(pc4), .eq(comparator_22_eq));  // open: gt, lt
  Comparator #(.width(32)) comparator_23 (.a(pastpc), .b(pc5), .eq(comparator_23_eq));  // open: gt, lt
  Comparator #(.width(32)) comparator_24 (.a(pastpc), .b(pc6), .eq(comparator_24_eq));  // open: gt, lt
  Comparator #(.width(32)) comparator_25 (.a(pastpc), .b(pc7), .eq(comparator_25_eq));  // open: gt, lt
  Multiplexer #(.width(32), .enable("false")) multiplexer_11 (
    .in0(multiplexer_10_out), .in1(addr2), .out(multiplexer_11_out), .sel(LH2));
  and and_27 (L0, V0, comparator_18_eq);
  and and_28 (L1, V1, comparator_19_eq);
  and and_29 (L2, V2, comparator_20_eq);
  and and_30 (L3, V3, comparator_21_eq);
  and and_31 (L4, V4, comparator_22_eq);
  and and_32 (L5, V5, comparator_23_eq);
  and and_33 (L6, V6, comparator_24_eq);
  and and_34 (L7, V7, comparator_25_eq);
  Multiplexer #(.width(32), .enable("false")) multiplexer_12 (
    .in0(multiplexer_11_out), .in1(addr3), .out(multiplexer_12_out), .sel(LH3));
  or or_5 (HIT2, L0, L1, L2, L3, L4, L5, L6, L7);
  Multiplexer #(.width(32), .enable("false")) multiplexer_13 (
    .in0(multiplexer_12_out), .in1(addr4), .out(multiplexer_13_out), .sel(LH4));
  Multiplexer #(.width(32), .enable("false")) multiplexer_14 (
    .in0(multiplexer_13_out), .in1(addr5), .out(multiplexer_14_out), .sel(LH5));
  Multiplexer #(.width(32), .enable("false")) multiplexer_15 (
    .in0(multiplexer_14_out), .in1(addr6), .out(multiplexer_15_out), .sel(LH6));
  Multiplexer #(.width(32), .enable("false")) multiplexer_16 (
    .in0(multiplexer_15_out), .in1(addr7), .out(pcout), .sel(LH7));
  Register #(.width(1)) register_1 (.D(1'b1), .en(SEL0), .Q(V0), .clk(CLK));  // open: clr
  Register #(.width(1)) register_2 (.D(1'b1), .en(SEL1), .Q(V1), .clk(CLK));  // open: clr
  Register #(.width(1)) register_3 (.D(1'b1), .en(SEL2), .Q(V2), .clk(CLK));  // open: clr
  Register #(.width(1)) register_4 (.D(1'b1), .en(SEL3), .Q(V3), .clk(CLK));  // open: clr
  Register #(.width(1)) register_5 (.D(1'b1), .en(SEL4), .Q(V4), .clk(CLK));  // open: clr
  Register #(.width(1)) register_6 (.D(1'b1), .en(SEL5), .Q(V5), .clk(CLK));  // open: clr
  Register #(.width(1)) register_7 (.D(1'b1), .en(SEL6), .Q(V6), .clk(CLK));  // open: clr
  Register #(.width(1)) register_8 (.D(1'b1), .en(SEL7), .Q(V7), .clk(CLK));  // open: clr
  Register #(.width(32)) register_9 (.D(pastpc), .en(SEL0), .Q(pc0), .clk(CLK));  // open: clr
  Register #(.width(32)) register_10 (.D(pastpc), .en(SEL1), .Q(pc1), .clk(CLK));  // open: clr
  Register #(.width(32)) register_11 (.D(pastpc), .en(SEL2), .Q(pc2), .clk(CLK));  // open: clr
  Register #(.width(32)) register_12 (.D(pastpc), .en(SEL3), .Q(pc3), .clk(CLK));  // open: clr
  Register #(.width(32)) register_13 (.D(pastpc), .en(SEL4), .Q(pc4), .clk(CLK));  // open: clr
  Register #(.width(32)) register_14 (.D(pastpc), .en(SEL5), .Q(pc5), .clk(CLK));  // open: clr
  Register #(.width(32)) register_15 (.D(pastpc), .en(SEL6), .Q(pc6), .clk(CLK));  // open: clr
  Register #(.width(32)) register_16 (.D(pastpc), .en(SEL7), .Q(pc7), .clk(CLK));  // open: clr
  Multiplexer #(.width(2), .enable("false")) multiplexer_17 (
    .in0(multiplexer_18_out), .in1(2'b01), .out(statein), .sel(and_35_out));
  and and_35 (and_35_out, ~HIT2, ~jump);  // AND_Gate
  \状态机  \u_状态机_1  (
    .\原预测状态高位 (stateout2[1]), .\原预测状态低位 (stateout2[0]), .\实际跳转情况 (and_36_out), .\新状态高位 (\状态机_1_新状态低位 [1]),
    .\新状态低位 (\状态机_1_新状态低位 [0]));
  and and_36 (and_36_out, jump2, jump);
  Register #(.width(2)) register_17 (.D(statein), .en(SEL0), .Q(register_17_q), .clk(CLK));  // open: clr
  Register #(.width(2)) register_18 (.D(statein), .en(SEL1), .Q(register_18_q), .clk(CLK));  // open: clr
  Register #(.width(2)) register_19 (.D(statein), .en(SEL2), .Q(register_19_q), .clk(CLK));  // open: clr
  Register #(.width(2)) register_20 (.D(statein), .en(SEL3), .Q(register_20_q), .clk(CLK));  // open: clr
  Register #(.width(2)) register_21 (.D(statein), .en(SEL4), .Q(register_21_q), .clk(CLK));  // open: clr
  Register #(.width(2)) register_22 (.D(statein), .en(SEL5), .Q(register_22_q), .clk(CLK));  // open: clr
  Register #(.width(2)) register_23 (.D(statein), .en(SEL6), .Q(register_23_q), .clk(CLK));  // open: clr
  Register #(.width(2)) register_24 (.D(statein), .en(SEL7), .Q(register_24_q), .clk(CLK));  // open: clr
  Multiplexer #(.width(2), .enable("false")) multiplexer_18 (
    .in0(\状态机_1_新状态低位 ), .in1(2'b11), .out(multiplexer_18_out), .sel(and_37_out));
  and and_37 (and_37_out, ~HIT2, jump);  // AND_Gate
  assign stateout1 = LH0 ? register_17_q : 2'bz;  // Controlled_Buffer controlled_buffer_3
  assign stateout2 = L0 ? register_17_q : 2'bz;  // Controlled_Buffer controlled_buffer_4
  assign stateout1 = LH1 ? register_18_q : 2'bz;  // Controlled_Buffer controlled_buffer_5
  assign stateout2 = L1 ? register_18_q : 2'bz;  // Controlled_Buffer controlled_buffer_6
  assign stateout1 = LH2 ? register_19_q : 2'bz;  // Controlled_Buffer controlled_buffer_7
  assign stateout2 = L2 ? register_19_q : 2'bz;  // Controlled_Buffer controlled_buffer_8
  assign stateout1 = LH3 ? register_20_q : 2'bz;  // Controlled_Buffer controlled_buffer_9
  assign stateout2 = L3 ? register_20_q : 2'bz;  // Controlled_Buffer controlled_buffer_10
  assign stateout1 = LH4 ? register_21_q : 2'bz;  // Controlled_Buffer controlled_buffer_11
  assign stateout2 = L4 ? register_21_q : 2'bz;  // Controlled_Buffer controlled_buffer_12
  assign stateout1 = LH5 ? register_22_q : 2'bz;  // Controlled_Buffer controlled_buffer_13
  assign stateout2 = L5 ? register_22_q : 2'bz;  // Controlled_Buffer controlled_buffer_14
  assign stateout1 = LH6 ? register_23_q : 2'bz;  // Controlled_Buffer controlled_buffer_15
  assign stateout2 = L6 ? register_23_q : 2'bz;  // Controlled_Buffer controlled_buffer_16
  assign stateout1 = LH7 ? register_24_q : 2'bz;  // Controlled_Buffer controlled_buffer_17
  assign stateout2 = L7 ? register_24_q : 2'bz;  // Controlled_Buffer controlled_buffer_18
  Counter #(.width(16), .max('hffff)) counter_1 (.count(HIT1), .Q(C0), .clk(CLK), .clr(L0));  // open: load, D, carry
  Counter #(.width(16), .max('hffff)) counter_2 (.count(HIT1), .Q(C1), .clk(CLK), .clr(L1));  // open: load, D, carry
  Counter #(.width(16), .max('hffff)) counter_3 (.count(HIT1), .Q(C2), .clk(CLK), .clr(L2));  // open: load, D, carry
  Counter #(.width(16), .max('hffff)) counter_4 (.count(HIT1), .Q(C3), .clk(CLK), .clr(L3));  // open: load, D, carry
  Counter #(.width(16), .max('hffff)) counter_5 (.count(HIT1), .Q(C4), .clk(CLK), .clr(L4));  // open: load, D, carry
  Counter #(.width(16), .max('hffff)) counter_6 (.count(HIT1), .Q(C5), .clk(CLK), .clr(L5));  // open: load, D, carry
  Counter #(.width(16), .max('hffff)) counter_7 (.count(HIT1), .Q(C6), .clk(CLK), .clr(L6));  // open: load, D, carry
  Counter #(.width(16), .max('hffff)) counter_8 (.count(HIT1), .Q(C7), .clk(CLK), .clr(L7));  // open: load, D, carry
  Register #(.width(32)) register_25 (.D(pastnpc), .en(SEL0), .Q(addr0), .clk(CLK));  // open: clr
  Register #(.width(32)) register_26 (.D(pastnpc), .en(SEL1), .Q(addr1), .clk(CLK));  // open: clr
  Register #(.width(32)) register_27 (.D(pastnpc), .en(SEL2), .Q(addr2), .clk(CLK));  // open: clr
  Register #(.width(32)) register_28 (.D(pastnpc), .en(SEL3), .Q(addr3), .clk(CLK));  // open: clr
  Register #(.width(32)) register_29 (.D(pastnpc), .en(SEL4), .Q(addr4), .clk(CLK));  // open: clr
  Register #(.width(32)) register_30 (.D(pastnpc), .en(SEL5), .Q(addr5), .clk(CLK));  // open: clr
  Register #(.width(32)) register_31 (.D(pastnpc), .en(SEL6), .Q(addr6), .clk(CLK));  // open: clr
  Register #(.width(32)) register_32 (.D(pastnpc), .en(SEL7), .Q(addr7), .clk(CLK));  // open: clr

  // Other names for the same wires on the sheet: functex[5:0] = EX_IR[5:0]; opex[5:0] = EX_IR[31:26];
  //   EX_pc[31:0] = pastpc; IF_pc[31:0] = pc; jump1 = jump

  // Notes on the sheet:
  //   有效位
  //   有效位
  //   有效位
  //   有效位
  //   有效位
  //   有效位
  //   有效位
  //   有效位
  //   标记位
  //   标记位
  //   标记位
  //   标记位
  //   标记位
  //   标记位
  //   标记位
  //   标记位
  //   淘汰标志位
  //   淘汰标志位
  //   淘汰标志位
  //   淘汰标志位
  //   淘汰标志位
  //   淘汰标志位
  //   淘汰标志位
  //   淘汰标志位
  //   数据块副本
  //   数据块副本
  //   数据块副本
  //   数据块副本
  //   数据块副本
  //   数据块副本
  //   数据块副本
  //   数据块副本
endmodule
